// Logisim project CompleteCircWithLayout.circ as structural Verilog: 12 circuits, main circuit main
// 4
module main (
);

  wire button_1_out, button_2_out, button_3_out, completecircuit_1_led;
  wire [3:0] completecircuit_1_minutes1, completecircuit_1_minutes2, completecircuit_1_second2,
       completecircuit_1_seconds1, completecircuit_1_split1, completecircuit_1_split2,
       completecircuit_1_split3, completecircuit_1_split4;

  Hex_Digit_Display hex_digit_display_1 (.value(completecircuit_1_minutes2));  // open: dp
  Hex_Digit_Display hex_digit_display_2 (.value(completecircuit_1_minutes1));  // open: dp
  Button button_1 (.out(button_1_out));
  Hex_Digit_Display hex_digit_display_3 (.value(completecircuit_1_second2));  // open: dp
  Button button_2 (.out(button_2_out));
  Hex_Digit_Display hex_digit_display_4 (.value(completecircuit_1_seconds1));  // open: dp
  CompleteCircuit completecircuit_1 (
    .RESET(button_3_out), .STARTSTOP(button_1_out), .SPLIT(button_2_out), .LED(completecircuit_1_led),
    .MINUTES2(completecircuit_1_minutes2), .MINUTES1(completecircuit_1_minutes1),
    .SECOND2(completecircuit_1_second2), .SECONDS1(completecircuit_1_seconds1),
    .SPLIT4(completecircuit_1_split4), .SPLIT3(completecircuit_1_split3), .SPLIT2(completecircuit_1_split2),
    .SPLIT1(completecircuit_1_split1));
  Button button_3 (.out(button_3_out));
  Hex_Digit_Display hex_digit_display_5 (.value(completecircuit_1_split4));  // open: dp
  Hex_Digit_Display hex_digit_display_6 (.value(completecircuit_1_split3));  // open: dp
  Hex_Digit_Display hex_digit_display_7 (.value(completecircuit_1_split2));  // open: dp
  LED led_1 (.in(completecircuit_1_led));
  Hex_Digit_Display hex_digit_display_8 (.value(completecircuit_1_split1));  // open: dp

  // Notes on the sheet:
  //   Minutes
  //   Start / Stop
  //   Elapsed Time
  //   Seconds
  //   :
  //   Stopwatch Interface
  //   Split
  //   Reset
  //   Minutes
  //   Split Time
  //   :
  //   Split Displayed
  //   Seconds
endmodule

module FourBitCounter (
  input  Reset,
  input  IncrementOne,
  input  IncrementTwo,
  input  CLK,
  input  StopCountImmediate,
  output ResetOut,
  output [3:0] HEX,
  output JKTwo,
  output JKEight,
  output BitOne,
  output BitTwo,
  output BitThree,
  output BitFour
);

  wire and_1_out, and_2_out, and_3_out, and_4_out, and_5_out, and_6_out, j_k_ff_1_q, j_k_ff_3_q, or_1_out;

  and and_1 (and_1_out, IncrementOne, IncrementTwo);
  J_K_Flip_Flop j_k_ff_1 (
    .J(and_1_out), .K(and_1_out), .clk(and_1_out), .Q(j_k_ff_1_q), .reset(or_1_out));  // open: Qn, preset
  and and_2 (and_2_out, CLK, StopCountImmediate);
  D_Flip_Flop d_ff_1 (.D(j_k_ff_1_q), .clk(and_2_out), .Q(BitOne), .reset(Reset));  // open: Qn, preset
  J_K_Flip_Flop j_k_ff_2 (
    .J(and_3_out), .K(and_3_out), .clk(and_1_out), .Q(JKTwo), .reset(or_1_out));  // open: Qn, preset
  buf and_3 (and_3_out, j_k_ff_1_q);  // AND_Gate
  and and_4 (and_4_out, and_3_out, JKTwo);
  D_Flip_Flop d_ff_2 (.D(JKTwo), .clk(and_2_out), .Q(BitTwo), .reset(Reset));  // open: Qn, preset
  J_K_Flip_Flop j_k_ff_3 (
    .J(and_4_out), .K(and_4_out), .clk(and_1_out), .Q(j_k_ff_3_q), .reset(or_1_out));  // open: Qn, preset
  and and_5 (and_5_out, and_4_out, j_k_ff_3_q);
  J_K_Flip_Flop j_k_ff_4 (
    .J(and_5_out), .K(and_5_out), .clk(and_1_out), .Q(JKEight), .reset(or_1_out));  // open: Qn, preset
  D_Flip_Flop d_ff_3 (.D(j_k_ff_3_q), .clk(and_2_out), .Q(BitThree), .reset(Reset));  // open: Qn, preset
  and and_6 (and_6_out, JKTwo, JKEight);
  or or_1 (or_1_out, and_6_out, Reset);
  D_Flip_Flop d_ff_4 (.D(JKEight), .clk(and_2_out), .Q(BitFour), .reset(Reset));  // open: Qn, preset

  assign HEX = {BitFour, BitThree, BitTwo, BitOne};
  assign ResetOut = Reset;

  // Notes on the sheet:
  //   Avoids illegal state
  //   OR for reset
endmodule

module ToggleFourBitCounter (
  input  Reset,
  input  StartStop,
  input  CLK,
  output ResetOut,
  output [3:0] HEX,
  output StopCountImmediateOut,
  output JKTwo,
  output JKEight,
  output BitOne,
  output BitTwo,
  output BitThree,
  output BitFour
);

  wire and_1_out, and_2_out, and_3_out, and_4_out, and_5_out, j_k_ff_1_q, j_k_ff_3_q, or_1_out;

  T_Flip_Flop t_ff_1 (.T(1'b1), .clk(StartStop), .Q(StopCountImmediateOut), .reset(Reset));  // open: Qn, preset
  J_K_Flip_Flop j_k_ff_1 (
    .J(StopCountImmediateOut), .K(StopCountImmediateOut), .clk(CLK), .Q(j_k_ff_1_q), .reset(or_1_out));  // open: Qn, preset
  and and_1 (and_1_out, StopCountImmediateOut, CLK);
  D_Flip_Flop d_ff_1 (.D(j_k_ff_1_q), .clk(and_1_out), .Q(BitOne), .reset(Reset));  // open: Qn, preset
  J_K_Flip_Flop j_k_ff_2 (.J(and_2_out), .K(and_2_out), .clk(CLK), .Q(JKTwo), .reset(or_1_out));  // open: Qn, preset
  and and_2 (and_2_out, StopCountImmediateOut, j_k_ff_1_q);
  D_Flip_Flop d_ff_2 (.D(JKTwo), .clk(and_1_out), .Q(BitTwo), .reset(Reset));  // open: Qn, preset
  and and_3 (and_3_out, and_2_out, JKTwo);
  J_K_Flip_Flop j_k_ff_3 (
    .J(and_3_out), .K(and_3_out), .clk(CLK), .Q(j_k_ff_3_q), .reset(or_1_out));  // open: Qn, preset
  and and_4 (and_4_out, and_3_out, j_k_ff_3_q);
  D_Flip_Flop d_ff_3 (.D(j_k_ff_3_q), .clk(and_1_out), .Q(BitThree), .reset(Reset));  // open: Qn, preset
  J_K_Flip_Flop j_k_ff_4 (.J(and_4_out), .K(and_4_out), .clk(CLK), .Q(JKEight), .reset(or_1_out));  // open: Qn, preset
  and and_5 (and_5_out, JKTwo, JKEight);
  or or_1 (or_1_out, and_5_out, Reset);
  D_Flip_Flop d_ff_4 (.D(JKEight), .clk(and_1_out), .Q(BitFour), .reset(Reset));  // open: Qn, preset

  assign HEX = {BitFour, BitThree, BitTwo, BitOne};
  assign ResetOut = Reset;

  // Notes on the sheet:
  //   Avoids illegal state
  //   OR for reset
endmodule

module ThreeBitCounterModulo6 (
  input  Reset,
  input  IncrementOne,
  input  IncrementTwo,
  input  CLK,
  output ResetOut,
  output [3:0] HEX,
  output JKTwo,
  output JkThree,
  output BitOne,
  output BitTwo,
  output BitThree
);

  wire and_1_out, and_2_out, and_3_out, j_k_ff_1_q, or_1_out;

  and and_1 (and_1_out, IncrementOne, IncrementTwo);
  J_K_Flip_Flop j_k_ff_1 (
    .J(and_1_out), .K(and_1_out), .clk(and_1_out), .Q(j_k_ff_1_q), .reset(or_1_out));  // open: Qn, preset
  D_Flip_Flop d_ff_1 (.D(j_k_ff_1_q), .clk(CLK), .Q(BitOne), .reset(Reset));  // open: Qn, preset
  J_K_Flip_Flop j_k_ff_2 (
    .J(j_k_ff_1_q), .K(j_k_ff_1_q), .clk(and_1_out), .Q(JKTwo), .reset(or_1_out));  // open: Qn, preset
  D_Flip_Flop d_ff_2 (.D(JKTwo), .clk(CLK), .Q(BitTwo), .reset(Reset));  // open: Qn, preset
  J_K_Flip_Flop j_k_ff_3 (
    .J(and_2_out), .K(and_2_out), .clk(and_1_out), .Q(JkThree), .reset(or_1_out));  // open: Qn, preset
  and and_2 (and_2_out, j_k_ff_1_q, JKTwo);
  D_Flip_Flop d_ff_3 (.D(JkThree), .clk(CLK), .Q(BitThree), .reset(Reset));  // open: Qn, preset
  and and_3 (and_3_out, JKTwo, JkThree);
  or or_1 (or_1_out, and_3_out, Reset);

  assign HEX = {1'b0, BitThree, BitTwo, BitOne};
  assign ResetOut = Reset;

  // Notes on the sheet:
  //   Seconds 02
  //   OR for reset
endmodule

module FourBitASyncRegister (
  input  BitOne,
  input  BitTwo,
  input  BitThree,
  input  BitFour,
  input  Reset,
  input  Split,
  output BitFourOut,
  output BitThreeOut,
  output BitTwoOut,
  output BitOneOut,
  output [3:0] HEX
);

  D_Flip_Flop d_ff_1 (.D(BitOne), .clk(Split), .Q(BitOneOut), .reset(Reset));  // open: Qn, preset
  D_Flip_Flop d_ff_2 (.D(BitTwo), .clk(Split), .Q(BitTwoOut), .reset(Reset));  // open: Qn, preset
  D_Flip_Flop d_ff_3 (.D(BitThree), .clk(Split), .Q(BitThreeOut), .reset(Reset));  // open: Qn, preset
  D_Flip_Flop d_ff_4 (.D(BitFour), .clk(Split), .Q(BitFourOut), .reset(Reset));  // open: Qn, preset

  assign HEX = {BitFourOut, BitThreeOut, BitTwoOut, BitOneOut};
endmodule

module ThreeBitASyncRegister (
  input  BitOne,
  input  BitTwo,
  input  BitThree,
  input  Reset,
  input  Split,
  output BitThreeOut,
  output BitTwoOut,
  output BitOneOut,
  output [3:0] HEX
);

  D_Flip_Flop d_ff_1 (.D(BitOne), .clk(Split), .Q(BitOneOut), .reset(Reset));  // open: Qn, preset
  D_Flip_Flop d_ff_2 (.D(BitTwo), .clk(Split), .Q(BitTwoOut), .reset(Reset));  // open: Qn, preset
  D_Flip_Flop d_ff_3 (.D(BitThree), .clk(Split), .Q(BitThreeOut), .reset(Reset));  // open: Qn, preset

  assign HEX = {1'b0, BitThreeOut, BitTwoOut, BitOneOut};
endmodule

module CircuitStage6b (
  input  RESET,
  input  StartStop,
  input  Split,
  output [3:0] ElapTimeSec2,
  output [3:0] ElapTimeMin2,
  output [3:0] ElapTimeSec1,
  output [3:0] ElapTimeMin1,
  output ToggleOnOffOut,
  output B1,
  output C1,
  output D1,
  output A1,
  output B2,
  output C2,
  output D2,
  output A2,
  output B3,
  output C3,
  output D3,
  output A3,
  output C4,
  output D4,
  output A4,
  output Ab1,
  output Bb1,
  output Cb1,
  output Db1,
  output Ab2,
  output Bb2,
  output Cb2,
  output Db2,
  output Ab3,
  output Bb3,
  output Cb3,
  output Db3,
  output Ab4,
  output Cb4,
  output Db4,
  output [3:0] SplitOut1,
  output [3:0] SplitOut2,
  output [3:0] SplitOut3,
  output [3:0] SplitOut4,
  output Ac1,
  output Bc1,
  output Cc1,
  output Dc1,
  output Ac2,
  output Bc2,
  output Cc2,
  output Dc2,
  output Ac3,
  output Bc3,
  output Cc3,
  output Dc3,
  output Ac4,
  output Cc4,
  output Dc4,
  output [3:0] Split1Out1,
  output [3:0] Split1Out2,
  output [3:0] Split1Out3,
  output [3:0] Split1Out4,
  output Ad1,
  output Bd1,
  output Cd1,
  output Dd1,
  output Ad2,
  output Bd2,
  output Cd2,
  output Dd2,
  output Ad3,
  output Bd3,
  output Cd3,
  output Dd3,
  output Ad4,
  output Cd4,
  output Dd4,
  output [3:0] Split2Out1,
  output [3:0] Split2Out2,
  output [3:0] Split2Out3,
  output [3:0] Split2Out4,
  output Ae1,
  output Be1,
  output Ce1,
  output De1,
  output Ae2,
  output Be2,
  output Ce2,
  output De2,
  output Ae3,
  output Be3,
  output Ce3,
  output De3,
  output Ae4,
  output Ce4,
  output De4,
  output [3:0] Split3Out1,
  output [3:0] Split3Out2,
  output [3:0] Split3Out3,
  output [3:0] Split3Out4,
  output Af1,
  output Bf1,
  output Cf1,
  output Df1,
  output Af2,
  output Bf2,
  output Cf2,
  output Df2,
  output Af3,
  output Bf3,
  output Cf3,
  output Df3,
  output Af4,
  output Cf4,
  output Df4,
  output [3:0] Split4Out1,
  output [3:0] Split4Out2,
  output [3:0] Split4Out3,
  output [3:0] Split4Out4
);

  wire clock_1_out, fourbitcounter_1_jkeight, fourbitcounter_1_jktwo, fourbitcounter_1_resetout, nand_1_out,
       nand_2_out, not_1_out, not_2_out, threebitcountermodulo6_1_jkthree, threebitcountermodulo6_1_jktwo,
       threebitcountermodulo6_1_resetout, togglefourbitcounter_1_jkeight, togglefourbitcounter_1_jktwo,
       togglefourbitcounter_1_resetout;

  nand nand_1 (nand_1_out, Split, nand_2_out);
  Clock clock_1 (.out(clock_1_out));
  not not_1 (not_1_out, nand_1_out);
  not not_2 (not_2_out, ToggleOnOffOut);
  nand nand_2 (nand_2_out, nand_1_out, not_2_out);
  ToggleFourBitCounter togglefourbitcounter_1 (
    .Reset(RESET), .StartStop(StartStop), .CLK(clock_1_out), .ResetOut(togglefourbitcounter_1_resetout),
    .HEX(ElapTimeSec1), .StopCountImmediateOut(ToggleOnOffOut), .JKTwo(togglefourbitcounter_1_jktwo),
    .JKEight(togglefourbitcounter_1_jkeight), .BitOne(A1), .BitTwo(A2), .BitThree(A3), .BitFour(A4));
  FourBitASyncRegister fourbitasyncregister_1 (
    .BitOne(A1), .BitTwo(A2), .BitThree(A3), .BitFour(A4), .Reset(RESET), .Split(not_1_out),
    .BitFourOut(Ab1), .BitThreeOut(Ab2), .BitTwoOut(Ab3), .BitOneOut(Ab4), .HEX(SplitOut1));
  FourBitASyncRegister fourbitasyncregister_2 (
    .BitOne(Ab4), .BitTwo(Ab3), .BitThree(Ab2), .BitFour(Ab1), .Reset(RESET), .Split(not_1_out),
    .BitFourOut(Ac1), .BitThreeOut(Ac2), .BitTwoOut(Ac3), .BitOneOut(Ac4), .HEX(Split1Out1));
  ThreeBitCounterModulo6 threebitcountermodulo6_1 (
    .Reset(togglefourbitcounter_1_resetout), .IncrementOne(togglefourbitcounter_1_jktwo),
    .IncrementTwo(togglefourbitcounter_1_jkeight), .CLK(clock_1_out),
    .ResetOut(threebitcountermodulo6_1_resetout), .HEX(ElapTimeSec2), .JKTwo(threebitcountermodulo6_1_jktwo),
    .JkThree(threebitcountermodulo6_1_jkthree), .BitOne(B1), .BitTwo(B2), .BitThree(B3));
  ThreeBitASyncRegister threebitasyncregister_1 (
    .BitOne(B1), .BitTwo(B2), .BitThree(B3), .Reset(RESET), .Split(not_1_out), .BitThreeOut(Bb1),
    .BitTwoOut(Bb2), .BitOneOut(Bb3), .HEX(SplitOut2));
  FourBitASyncRegister fourbitasyncregister_3 (
    .BitOne(Ac4), .BitTwo(Ac3), .BitThree(Ac2), .BitFour(Ac1), .Reset(RESET), .Split(not_1_out),
    .BitFourOut(Ad1), .BitThreeOut(Ad2), .BitTwoOut(Ad3), .BitOneOut(Ad4), .HEX(Split2Out1));
  ThreeBitASyncRegister threebitasyncregister_2 (
    .BitOne(Bb3), .BitTwo(Bb2), .BitThree(Bb1), .Reset(RESET), .Split(not_1_out), .BitThreeOut(Bc1),
    .BitTwoOut(Bc2), .BitOneOut(Bc3), .HEX(Split1Out2));
  FourBitCounter fourbitcounter_1 (
    .Reset(threebitcountermodulo6_1_resetout), .IncrementOne(threebitcountermodulo6_1_jktwo),
    .IncrementTwo(threebitcountermodulo6_1_jkthree), .CLK(clock_1_out), .StopCountImmediate(ToggleOnOffOut),
    .ResetOut(fourbitcounter_1_resetout), .HEX(ElapTimeMin1), .JKTwo(fourbitcounter_1_jktwo),
    .JKEight(fourbitcounter_1_jkeight), .BitOne(C1), .BitTwo(C2), .BitThree(C3), .BitFour(C4));
  FourBitASyncRegister fourbitasyncregister_4 (
    .BitOne(C1), .BitTwo(C2), .BitThree(C3), .BitFour(C4), .Reset(RESET), .Split(not_1_out),
    .BitFourOut(Cb1), .BitThreeOut(Cb2), .BitTwoOut(Cb3), .BitOneOut(Cb4), .HEX(SplitOut3));
  FourBitASyncRegister fourbitasyncregister_5 (
    .BitOne(Ad4), .BitTwo(Ad3), .BitThree(Ad2), .BitFour(Ad1), .Reset(RESET), .Split(not_1_out),
    .BitFourOut(Ae1), .BitThreeOut(Ae2), .BitTwoOut(Ae3), .BitOneOut(Ae4), .HEX(Split3Out1));
  ThreeBitASyncRegister threebitasyncregister_3 (
    .BitOne(Bc3), .BitTwo(Bc2), .BitThree(Bc1), .Reset(RESET), .Split(not_1_out), .BitThreeOut(Bd1),
    .BitTwoOut(Bd2), .BitOneOut(Bd3), .HEX(Split2Out2));
  FourBitASyncRegister fourbitasyncregister_6 (
    .BitOne(Cb4), .BitTwo(Cb3), .BitThree(Cb2), .BitFour(Cb1), .Reset(RESET), .Split(not_1_out),
    .BitFourOut(Cc1), .BitThreeOut(Cc2), .BitTwoOut(Cc3), .BitOneOut(Cc4), .HEX(Split1Out3));
  FourBitCounter fourbitcounter_2 (
    .Reset(fourbitcounter_1_resetout), .IncrementOne(fourbitcounter_1_jktwo),
    .IncrementTwo(fourbitcounter_1_jkeight), .CLK(clock_1_out), .StopCountImmediate(ToggleOnOffOut),
    .HEX(ElapTimeMin2), .BitOne(D1), .BitTwo(D2), .BitThree(D3), .BitFour(D4));  // open: ResetOut, JKTwo, JKEight
  FourBitASyncRegister fourbitasyncregister_7 (
    .BitOne(D1), .BitTwo(D2), .BitThree(D3), .BitFour(D4), .Reset(RESET), .Split(not_1_out),
    .BitFourOut(Db1), .BitThreeOut(Db2), .BitTwoOut(Db3), .BitOneOut(Db4), .HEX(SplitOut4));
  FourBitASyncRegister fourbitasyncregister_8 (
    .BitOne(Ae4), .BitTwo(Ae3), .BitThree(Ae2), .BitFour(Ae1), .Reset(RESET), .Split(not_1_out),
    .BitFourOut(Af1), .BitThreeOut(Af2), .BitTwoOut(Af3), .BitOneOut(Af4), .HEX(Split4Out1));
  ThreeBitASyncRegister threebitasyncregister_4 (
    .BitOne(Bd3), .BitTwo(Bd2), .BitThree(Bd1), .Reset(RESET), .Split(not_1_out), .BitThreeOut(Be1),
    .BitTwoOut(Be2), .BitOneOut(Be3), .HEX(Split3Out2));
  FourBitASyncRegister fourbitasyncregister_9 (
    .BitOne(Cc4), .BitTwo(Cc3), .BitThree(Cc2), .BitFour(Cc1), .Reset(RESET), .Split(not_1_out),
    .BitFourOut(Cd1), .BitThreeOut(Cd2), .BitTwoOut(Cd3), .BitOneOut(Cd4), .HEX(Split2Out3));
  FourBitASyncRegister fourbitasyncregister_10 (
    .BitOne(Db4), .BitTwo(Db3), .BitThree(Db2), .BitFour(Db1), .Reset(RESET), .Split(not_1_out),
    .BitFourOut(Dc1), .BitThreeOut(Dc2), .BitTwoOut(Dc3), .BitOneOut(Dc4), .HEX(Split1Out4));
  ThreeBitASyncRegister threebitasyncregister_5 (
    .BitOne(Be3), .BitTwo(Be2), .BitThree(Be1), .Reset(RESET), .Split(not_1_out), .BitThreeOut(Bf1),
    .BitTwoOut(Bf2), .BitOneOut(Bf3), .HEX(Split4Out2));
  FourBitASyncRegister fourbitasyncregister_11 (
    .BitOne(Cd4), .BitTwo(Cd3), .BitThree(Cd2), .BitFour(Cd1), .Reset(RESET), .Split(not_1_out),
    .BitFourOut(Ce1), .BitThreeOut(Ce2), .BitTwoOut(Ce3), .BitOneOut(Ce4), .HEX(Split3Out3));
  FourBitASyncRegister fourbitasyncregister_12 (
    .BitOne(Dc4), .BitTwo(Dc3), .BitThree(Dc2), .BitFour(Dc1), .Reset(RESET), .Split(not_1_out),
    .BitFourOut(Dd1), .BitThreeOut(Dd2), .BitTwoOut(Dd3), .BitOneOut(Dd4), .HEX(Split2Out4));
  FourBitASyncRegister fourbitasyncregister_13 (
    .BitOne(Ce4), .BitTwo(Ce3), .BitThree(Ce2), .BitFour(Ce1), .Reset(RESET), .Split(not_1_out),
    .BitFourOut(Cf1), .BitThreeOut(Cf2), .BitTwoOut(Cf3), .BitOneOut(Cf4), .HEX(Split4Out3));
  FourBitASyncRegister fourbitasyncregister_14 (
    .BitOne(Dd4), .BitTwo(Dd3), .BitThree(Dd2), .BitFour(Dd1), .Reset(RESET), .Split(not_1_out),
    .BitFourOut(De1), .BitThreeOut(De2), .BitTwoOut(De3), .BitOneOut(De4), .HEX(Split3Out4));
  FourBitASyncRegister fourbitasyncregister_15 (
    .BitOne(De4), .BitTwo(De3), .BitThree(De2), .BitFour(De1), .Reset(RESET), .Split(not_1_out),
    .BitFourOut(Df1), .BitThreeOut(Df2), .BitTwoOut(Df3), .BitOneOut(Df4), .HEX(Split4Out4));
endmodule

module FiveInputMultiplexer (
  input  BitThree,
  input  BitTwo,
  input  BitOne,
  input  Input5,
  input  Input4,
  input  Input3,
  input  Input2,
  input  Input1,
  output Multiout
);

  wire and_1_out, and_2_out, and_3_out, and_4_out, and_5_out, not_1_out, not_2_out, not_3_out;

  and and_1 (and_1_out, BitThree, not_2_out, not_3_out, Input5);
  not not_1 (not_1_out, BitThree);
  not not_2 (not_2_out, BitTwo);
  not not_3 (not_3_out, BitOne);
  and and_2 (and_2_out, BitOne, BitTwo, not_1_out, Input4);
  or or_1 (Multiout, and_1_out, and_2_out, and_4_out, and_3_out, and_5_out);
  and and_3 (and_3_out, not_1_out, not_2_out, BitOne, Input2);
  and and_4 (and_4_out, BitTwo, not_1_out, not_3_out, Input3);
  and and_5 (and_5_out, not_1_out, not_2_out, not_3_out, Input1);
endmodule

module FiveAsyncModCounter (
  input  CLK,
  input  Reset,
  output Output1,
  output Output2,
  output Output3
);

  wire and_1_out, or_1_out;

  J_K_Flip_Flop #(.trigger("falling")) j_k_ff_1 (
    .J(1'b1), .K(1'b1), .clk(CLK), .Q(Output1), .reset(or_1_out));  // open: Qn, preset
  J_K_Flip_Flop #(.trigger("falling")) j_k_ff_2 (
    .J(1'b1), .K(1'b1), .clk(Output1), .Q(Output2), .reset(or_1_out));  // open: Qn, preset
  J_K_Flip_Flop #(.trigger("falling")) j_k_ff_3 (
    .J(Output2), .K(Output2), .clk(Output1), .Q(Output3), .reset(or_1_out));  // open: Qn, preset
  or or_1 (or_1_out, and_1_out, Reset);
  and and_1 (and_1_out, Output1, Output3);
endmodule

module SixAsyncModCounter (
  input  ResetForNoSplit,
  input  CLK,
  input  Reset,
  output LED,
  output Output1,
  output Output2,
  output Output3
);

  wire and_1_out, and_2_out, and_3_out, or_2_out;

  J_K_Flip_Flop #(.trigger("falling")) j_k_ff_1 (
    .J(1'b1), .K(1'b1), .clk(CLK), .Q(Output1), .reset(or_2_out));  // open: Qn, preset
  J_K_Flip_Flop #(.trigger("falling")) j_k_ff_2 (
    .J(1'b1), .K(1'b1), .clk(Output1), .Q(Output2), .reset(or_2_out));  // open: Qn, preset
  or or_1 (LED, Output1, Output2, Output3);
  J_K_Flip_Flop #(.trigger("falling")) j_k_ff_3 (
    .J(Output2), .K(Output2), .clk(Output1), .Q(Output3), .reset(or_2_out));  // open: Qn, preset
  or or_2 (or_2_out, and_1_out, and_3_out, Reset);
  and and_1 (and_1_out, Output2, Output3);
  and and_2 (and_2_out, LED, LED, ResetForNoSplit);
  and and_3 (and_3_out, and_2_out, ResetForNoSplit);

  // Notes on the sheet:
  //   2 AND gates to elimainate momentary ellegal state
endmodule

module SixInputMultiplexer (
  input  BitThree,
  input  BitTwo,
  input  BitOne,
  input  Input5,
  input  Input4,
  input  Input3,
  input  Input2,
  input  Input1,
  input  InputTimer,
  output MultiOut
);

  wire and_1_out, and_2_out, and_3_out, and_4_out, and_5_out, and_6_out, not_1_out, not_2_out, not_3_out;

  and and_1 (and_1_out, BitOne, not_2_out, BitThree, Input5);
  not not_1 (not_1_out, BitThree);
  not not_2 (not_2_out, BitTwo);
  not not_3 (not_3_out, BitOne);
  and and_2 (and_2_out, BitThree, not_2_out, not_3_out, Input4);
  and and_3 (and_3_out, BitOne, BitTwo, not_1_out, Input3);
  or m04 (MultiOut, and_1_out, and_2_out, and_3_out, and_4_out, and_5_out, and_6_out);
  and and_4 (and_4_out, BitTwo, not_1_out, not_3_out, Input2);
  and and_5 (and_5_out, not_1_out, not_2_out, BitOne, Input1);
  and and_6 (and_6_out, not_1_out, not_2_out, not_3_out, InputTimer);
endmodule

module CompleteCircuit (
  input  RESET,
  input  STARTSTOP,
  input  SPLIT,
  output LED,
  output [3:0] MINUTES2,
  output [3:0] MINUTES1,
  output [3:0] SECOND2,
  output [3:0] SECONDS1,
  output [3:0] SPLIT4,
  output [3:0] SPLIT3,
  output [3:0] SPLIT2,
  output [3:0] SPLIT1
);

  wire circuitstage6b_1_a1, circuitstage6b_1_a2, circuitstage6b_1_a3, circuitstage6b_1_a4,
       circuitstage6b_1_ab1, circuitstage6b_1_ab2, circuitstage6b_1_ab3, circuitstage6b_1_ab4,
       circuitstage6b_1_ac1, circuitstage6b_1_ac2, circuitstage6b_1_ac3, circuitstage6b_1_ac4,
       circuitstage6b_1_ad1, circuitstage6b_1_ad2, circuitstage6b_1_ad3, circuitstage6b_1_ad4,
       circuitstage6b_1_ae1, circuitstage6b_1_ae2, circuitstage6b_1_ae3, circuitstage6b_1_ae4,
       circuitstage6b_1_af1, circuitstage6b_1_af2, circuitstage6b_1_af3, circuitstage6b_1_af4,
       circuitstage6b_1_b1, circuitstage6b_1_b2, circuitstage6b_1_b3, circuitstage6b_1_bb1,
       circuitstage6b_1_bb2, circuitstage6b_1_bb3, circuitstage6b_1_bc1, circuitstage6b_1_bc2,
       circuitstage6b_1_bc3, circuitstage6b_1_bd1, circuitstage6b_1_bd2, circuitstage6b_1_bd3,
       circuitstage6b_1_be1, circuitstage6b_1_be2, circuitstage6b_1_be3, circuitstage6b_1_bf1,
       circuitstage6b_1_bf2, circuitstage6b_1_bf3, circuitstage6b_1_c1, circuitstage6b_1_c2,
       circuitstage6b_1_c3, circuitstage6b_1_c4, circuitstage6b_1_cb1, circuitstage6b_1_cb2,
       circuitstage6b_1_cb3, circuitstage6b_1_cb4, circuitstage6b_1_cc1, circuitstage6b_1_cc2,
       circuitstage6b_1_cc3, circuitstage6b_1_cc4, circuitstage6b_1_cd1, circuitstage6b_1_cd2,
       circuitstage6b_1_cd3, circuitstage6b_1_cd4, circuitstage6b_1_ce1, circuitstage6b_1_ce2,
       circuitstage6b_1_ce3, circuitstage6b_1_ce4, circuitstage6b_1_cf1, circuitstage6b_1_cf2,
       circuitstage6b_1_cf3, circuitstage6b_1_cf4, circuitstage6b_1_d1, circuitstage6b_1_d2,
       circuitstage6b_1_d3, circuitstage6b_1_d4, circuitstage6b_1_db1, circuitstage6b_1_db2,
       circuitstage6b_1_db3, circuitstage6b_1_db4, circuitstage6b_1_dc1, circuitstage6b_1_dc2,
       circuitstage6b_1_dc3, circuitstage6b_1_dc4, circuitstage6b_1_dd1, circuitstage6b_1_dd2,
       circuitstage6b_1_dd3, circuitstage6b_1_dd4, circuitstage6b_1_de1, circuitstage6b_1_de2,
       circuitstage6b_1_de3, circuitstage6b_1_de4, circuitstage6b_1_df1, circuitstage6b_1_df2,
       circuitstage6b_1_df3, circuitstage6b_1_df4, circuitstage6b_1_toggleonoffout, nand_1_out, nand_2_out,
       nor_1_out, or_1_out, or_2_out, or_3_out, or_4_out, sixasyncmodcounter_1_output1,
       sixasyncmodcounter_1_output2, sixasyncmodcounter_1_output3;
  wire [3:0] circuitstage6b_1_split1out1, circuitstage6b_1_split1out2, circuitstage6b_1_split1out3,
       circuitstage6b_1_split1out4, circuitstage6b_1_split2out1, circuitstage6b_1_split2out2,
       circuitstage6b_1_split2out3, circuitstage6b_1_split2out4, circuitstage6b_1_split3out1,
       circuitstage6b_1_split3out2, circuitstage6b_1_split3out3, circuitstage6b_1_split3out4,
       circuitstage6b_1_split4out1, circuitstage6b_1_split4out2, circuitstage6b_1_split4out3,
       circuitstage6b_1_split4out4;

  nand nand_1 (nand_1_out, SPLIT, nand_2_out);
  Hex_Digit_Display hex_digit_display_1 (.value(circuitstage6b_1_split1out4));  // open: dp
  Hex_Digit_Display hex_digit_display_2 (.value(circuitstage6b_1_split2out4));  // open: dp
  Hex_Digit_Display hex_digit_display_3 (.value(circuitstage6b_1_split3out4));  // open: dp
  Hex_Digit_Display hex_digit_display_4 (.value(circuitstage6b_1_split4out4));  // open: dp
  nand nand_2 (nand_2_out, nand_1_out, circuitstage6b_1_toggleonoffout);
  Hex_Digit_Display hex_digit_display_5 (.value(circuitstage6b_1_split1out3));  // open: dp
  Hex_Digit_Display hex_digit_display_6 (.value(circuitstage6b_1_split1out2));  // open: dp
  Hex_Digit_Display hex_digit_display_7 (.value(circuitstage6b_1_split2out3));  // open: dp
  Hex_Digit_Display hex_digit_display_8 (.value(circuitstage6b_1_split3out3));  // open: dp
  Hex_Digit_Display hex_digit_display_9 (.value(circuitstage6b_1_split4out3));  // open: dp
  Hex_Digit_Display hex_digit_display_10 (.value(circuitstage6b_1_split1out1));  // open: dp
  Hex_Digit_Display hex_digit_display_11 (.value(circuitstage6b_1_split2out2));  // open: dp
  Hex_Digit_Display hex_digit_display_12 (.value(circuitstage6b_1_split2out1));  // open: dp
  Hex_Digit_Display hex_digit_display_13 (.value(circuitstage6b_1_split3out2));  // open: dp
  Hex_Digit_Display hex_digit_display_14 (.value(circuitstage6b_1_split3out1));  // open: dp
  Hex_Digit_Display hex_digit_display_15 (.value(circuitstage6b_1_split4out2));  // open: dp
  Hex_Digit_Display hex_digit_display_16 (.value(circuitstage6b_1_split4out1));  // open: dp
  or or_1 (or_1_out, RESET, STARTSTOP);
  CircuitStage6b circuitstage6b_1 (
    .RESET(RESET), .StartStop(STARTSTOP), .Split(SPLIT), .ToggleOnOffOut(circuitstage6b_1_toggleonoffout),
    .B1(circuitstage6b_1_b1), .C1(circuitstage6b_1_c1), .D1(circuitstage6b_1_d1), .A1(circuitstage6b_1_a1),
    .B2(circuitstage6b_1_b2), .C2(circuitstage6b_1_c2), .D2(circuitstage6b_1_d2), .A2(circuitstage6b_1_a2),
    .B3(circuitstage6b_1_b3), .C3(circuitstage6b_1_c3), .D3(circuitstage6b_1_d3), .A3(circuitstage6b_1_a3),
    .C4(circuitstage6b_1_c4), .D4(circuitstage6b_1_d4), .A4(circuitstage6b_1_a4), .Ab1(circuitstage6b_1_ab1),
    .Bb1(circuitstage6b_1_bb1), .Cb1(circuitstage6b_1_cb1), .Db1(circuitstage6b_1_db1),
    .Ab2(circuitstage6b_1_ab2), .Bb2(circuitstage6b_1_bb2), .Cb2(circuitstage6b_1_cb2),
    .Db2(circuitstage6b_1_db2), .Ab3(circuitstage6b_1_ab3), .Bb3(circuitstage6b_1_bb3),
    .Cb3(circuitstage6b_1_cb3), .Db3(circuitstage6b_1_db3), .Ab4(circuitstage6b_1_ab4),
    .Cb4(circuitstage6b_1_cb4), .Db4(circuitstage6b_1_db4), .SplitOut1(SPLIT1), .SplitOut2(SPLIT2),
    .SplitOut3(SPLIT3), .SplitOut4(SPLIT4), .Ac1(circuitstage6b_1_ac1), .Bc1(circuitstage6b_1_bc1),
    .Cc1(circuitstage6b_1_cc1), .Dc1(circuitstage6b_1_dc1), .Ac2(circuitstage6b_1_ac2),
    .Bc2(circuitstage6b_1_bc2), .Cc2(circuitstage6b_1_cc2), .Dc2(circuitstage6b_1_dc2),
    .Ac3(circuitstage6b_1_ac3), .Bc3(circuitstage6b_1_bc3), .Cc3(circuitstage6b_1_cc3),
    .Dc3(circuitstage6b_1_dc3), .Ac4(circuitstage6b_1_ac4), .Cc4(circuitstage6b_1_cc4),
    .Dc4(circuitstage6b_1_dc4), .Split1Out1(circuitstage6b_1_split1out1),
    .Split1Out2(circuitstage6b_1_split1out2), .Split1Out3(circuitstage6b_1_split1out3),
    .Split1Out4(circuitstage6b_1_split1out4), .Ad1(circuitstage6b_1_ad1), .Bd1(circuitstage6b_1_bd1),
    .Cd1(circuitstage6b_1_cd1), .Dd1(circuitstage6b_1_dd1), .Ad2(circuitstage6b_1_ad2),
    .Bd2(circuitstage6b_1_bd2), .Cd2(circuitstage6b_1_cd2), .Dd2(circuitstage6b_1_dd2),
    .Ad3(circuitstage6b_1_ad3), .Bd3(circuitstage6b_1_bd3), .Cd3(circuitstage6b_1_cd3),
    .Dd3(circuitstage6b_1_dd3), .Ad4(circuitstage6b_1_ad4), .Cd4(circuitstage6b_1_cd4),
    .Dd4(circuitstage6b_1_dd4), .Split2Out1(circuitstage6b_1_split2out1),
    .Split2Out2(circuitstage6b_1_split2out2), .Split2Out3(circuitstage6b_1_split2out3),
    .Split2Out4(circuitstage6b_1_split2out4), .Ae1(circuitstage6b_1_ae1), .Be1(circuitstage6b_1_be1),
    .Ce1(circuitstage6b_1_ce1), .De1(circuitstage6b_1_de1), .Ae2(circuitstage6b_1_ae2),
    .Be2(circuitstage6b_1_be2), .Ce2(circuitstage6b_1_ce2), .De2(circuitstage6b_1_de2),
    .Ae3(circuitstage6b_1_ae3), .Be3(circuitstage6b_1_be3), .Ce3(circuitstage6b_1_ce3),
    .De3(circuitstage6b_1_de3), .Ae4(circuitstage6b_1_ae4), .Ce4(circuitstage6b_1_ce4),
    .De4(circuitstage6b_1_de4), .Split3Out1(circuitstage6b_1_split3out1),
    .Split3Out2(circuitstage6b_1_split3out2), .Split3Out3(circuitstage6b_1_split3out3),
    .Split3Out4(circuitstage6b_1_split3out4), .Af1(circuitstage6b_1_af1), .Bf1(circuitstage6b_1_bf1),
    .Cf1(circuitstage6b_1_cf1), .Df1(circuitstage6b_1_df1), .Af2(circuitstage6b_1_af2),
    .Bf2(circuitstage6b_1_bf2), .Cf2(circuitstage6b_1_cf2), .Df2(circuitstage6b_1_df2),
    .Af3(circuitstage6b_1_af3), .Bf3(circuitstage6b_1_bf3), .Cf3(circuitstage6b_1_cf3),
    .Df3(circuitstage6b_1_df3), .Af4(circuitstage6b_1_af4), .Cf4(circuitstage6b_1_cf4),
    .Df4(circuitstage6b_1_df4), .Split4Out1(circuitstage6b_1_split4out1),
    .Split4Out2(circuitstage6b_1_split4out2), .Split4Out3(circuitstage6b_1_split4out3),
    .Split4Out4(circuitstage6b_1_split4out4));  // open: ElapTimeSec2, ElapTimeMin2, ElapTimeSec1, ElapTimeMin1
  SixAsyncModCounter sixasyncmodcounter_1 (
    .ResetForNoSplit(nor_1_out), .CLK(nand_1_out), .Reset(or_1_out), .LED(LED),
    .Output1(sixasyncmodcounter_1_output1), .Output2(sixasyncmodcounter_1_output2),
    .Output3(sixasyncmodcounter_1_output3));
  nor nor_1 (nor_1_out, or_2_out, SECONDS1[3], SECONDS1[2], SECONDS1[1], SECONDS1[0]);
  SixInputMultiplexer sixinputmultiplexer_1 (
    .BitThree(sixasyncmodcounter_1_output3), .BitTwo(sixasyncmodcounter_1_output2),
    .BitOne(sixasyncmodcounter_1_output1), .Input5(circuitstage6b_1_af4), .Input4(circuitstage6b_1_ae4),
    .Input3(circuitstage6b_1_ad4), .Input2(circuitstage6b_1_ac4), .Input1(circuitstage6b_1_ab4),
    .InputTimer(circuitstage6b_1_a1), .MultiOut(SECONDS1[0]));
  SixInputMultiplexer sixinputmultiplexer_2 (
    .BitThree(sixasyncmodcounter_1_output3), .BitTwo(sixasyncmodcounter_1_output2),
    .BitOne(sixasyncmodcounter_1_output1), .Input5(circuitstage6b_1_bf3), .Input4(circuitstage6b_1_be3),
    .Input3(circuitstage6b_1_bd3), .Input2(circuitstage6b_1_bc3), .Input1(circuitstage6b_1_bb3),
    .InputTimer(circuitstage6b_1_b1), .MultiOut(SECOND2[0]));
  SixInputMultiplexer sixinputmultiplexer_3 (
    .BitThree(sixasyncmodcounter_1_output3), .BitTwo(sixasyncmodcounter_1_output2),
    .BitOne(sixasyncmodcounter_1_output1), .Input5(circuitstage6b_1_cf4), .Input4(circuitstage6b_1_ce4),
    .Input3(circuitstage6b_1_cd4), .Input2(circuitstage6b_1_cc4), .Input1(circuitstage6b_1_cb4),
    .InputTimer(circuitstage6b_1_c1), .MultiOut(MINUTES1[0]));
  SixInputMultiplexer sixinputmultiplexer_4 (
    .BitThree(sixasyncmodcounter_1_output3), .BitTwo(sixasyncmodcounter_1_output2),
    .BitOne(sixasyncmodcounter_1_output1), .Input5(circuitstage6b_1_af3), .Input4(circuitstage6b_1_ae3),
    .Input3(circuitstage6b_1_ad3), .Input2(circuitstage6b_1_ac3), .Input1(circuitstage6b_1_ab3),
    .InputTimer(circuitstage6b_1_a2), .MultiOut(SECONDS1[1]));
  SixInputMultiplexer sixinputmultiplexer_5 (
    .BitThree(sixasyncmodcounter_1_output3), .BitTwo(sixasyncmodcounter_1_output2),
    .BitOne(sixasyncmodcounter_1_output1), .Input5(circuitstage6b_1_df4), .Input4(circuitstage6b_1_de4),
    .Input3(circuitstage6b_1_dd4), .Input2(circuitstage6b_1_dc4), .Input1(circuitstage6b_1_db4),
    .InputTimer(circuitstage6b_1_d1), .MultiOut(MINUTES2[0]));
  SixInputMultiplexer sixinputmultiplexer_6 (
    .BitThree(sixasyncmodcounter_1_output3), .BitTwo(sixasyncmodcounter_1_output2),
    .BitOne(sixasyncmodcounter_1_output1), .Input5(circuitstage6b_1_bf2), .Input4(circuitstage6b_1_be2),
    .Input3(circuitstage6b_1_bd2), .Input2(circuitstage6b_1_bc2), .Input1(circuitstage6b_1_bb2),
    .InputTimer(circuitstage6b_1_b2), .MultiOut(SECOND2[1]));
  SixInputMultiplexer sixinputmultiplexer_7 (
    .BitThree(sixasyncmodcounter_1_output3), .BitTwo(sixasyncmodcounter_1_output2),
    .BitOne(sixasyncmodcounter_1_output1), .Input5(circuitstage6b_1_af2), .Input4(circuitstage6b_1_ae2),
    .Input3(circuitstage6b_1_ad2), .Input2(circuitstage6b_1_ac2), .Input1(circuitstage6b_1_ab2),
    .InputTimer(circuitstage6b_1_a3), .MultiOut(SECONDS1[2]));
  SixInputMultiplexer sixinputmultiplexer_8 (
    .BitThree(sixasyncmodcounter_1_output3), .BitTwo(sixasyncmodcounter_1_output2),
    .BitOne(sixasyncmodcounter_1_output1), .Input5(circuitstage6b_1_cf3), .Input4(circuitstage6b_1_ce3),
    .Input3(circuitstage6b_1_cd3), .Input2(circuitstage6b_1_cc3), .Input1(circuitstage6b_1_cb3),
    .InputTimer(circuitstage6b_1_c2), .MultiOut(MINUTES1[1]));
  SixInputMultiplexer sixinputmultiplexer_9 (
    .BitThree(sixasyncmodcounter_1_output3), .BitTwo(sixasyncmodcounter_1_output2),
    .BitOne(sixasyncmodcounter_1_output1), .Input5(circuitstage6b_1_df3), .Input4(circuitstage6b_1_de3),
    .Input3(circuitstage6b_1_dd3), .Input2(circuitstage6b_1_dc3), .Input1(circuitstage6b_1_db3),
    .InputTimer(circuitstage6b_1_d2), .MultiOut(MINUTES2[1]));
  SixInputMultiplexer sixinputmultiplexer_10 (
    .BitThree(sixasyncmodcounter_1_output3), .BitTwo(sixasyncmodcounter_1_output2),
    .BitOne(sixasyncmodcounter_1_output1), .Input5(circuitstage6b_1_af1), .Input4(circuitstage6b_1_ae1),
    .Input3(circuitstage6b_1_ad1), .Input2(circuitstage6b_1_ac1), .Input1(circuitstage6b_1_ab1),
    .InputTimer(circuitstage6b_1_a4), .MultiOut(SECONDS1[3]));
  or or_2 (or_2_out, SECOND2[1], or_3_out, SECOND2[2], SECOND2[0]);
  SixInputMultiplexer sixinputmultiplexer_11 (
    .BitThree(sixasyncmodcounter_1_output3), .BitTwo(sixasyncmodcounter_1_output2),
    .BitOne(sixasyncmodcounter_1_output1), .Input5(circuitstage6b_1_bf1), .Input4(circuitstage6b_1_be1),
    .Input3(circuitstage6b_1_bd1), .Input2(circuitstage6b_1_bc1), .Input1(circuitstage6b_1_bb1),
    .InputTimer(circuitstage6b_1_b3), .MultiOut(SECOND2[2]));
  SixInputMultiplexer sixinputmultiplexer_12 (
    .BitThree(sixasyncmodcounter_1_output3), .BitTwo(sixasyncmodcounter_1_output2),
    .BitOne(sixasyncmodcounter_1_output1), .Input5(circuitstage6b_1_cf2), .Input4(circuitstage6b_1_ce2),
    .Input3(circuitstage6b_1_cd2), .Input2(circuitstage6b_1_cc2), .Input1(circuitstage6b_1_cb2),
    .InputTimer(circuitstage6b_1_c3), .MultiOut(MINUTES1[2]));
  or or_3 (or_3_out, MINUTES1[0], MINUTES1[1], or_4_out, MINUTES1[2], MINUTES1[3]);
  SixInputMultiplexer sixinputmultiplexer_13 (
    .BitThree(sixasyncmodcounter_1_output3), .BitTwo(sixasyncmodcounter_1_output2),
    .BitOne(sixasyncmodcounter_1_output1), .Input5(circuitstage6b_1_df2), .Input4(circuitstage6b_1_de2),
    .Input3(circuitstage6b_1_dd2), .Input2(circuitstage6b_1_dc2), .Input1(circuitstage6b_1_db2),
    .InputTimer(circuitstage6b_1_d3), .MultiOut(MINUTES2[2]));
  SixInputMultiplexer sixinputmultiplexer_14 (
    .BitThree(sixasyncmodcounter_1_output3), .BitTwo(sixasyncmodcounter_1_output2),
    .BitOne(sixasyncmodcounter_1_output1), .Input5(circuitstage6b_1_cf1), .Input4(circuitstage6b_1_ce1),
    .Input3(circuitstage6b_1_cd1), .Input2(circuitstage6b_1_cc1), .Input1(circuitstage6b_1_cb1),
    .InputTimer(circuitstage6b_1_c4), .MultiOut(MINUTES1[3]));
  or or_4 (or_4_out, MINUTES2[0], MINUTES2[1], MINUTES2[2], MINUTES2[3]);
  SixInputMultiplexer sixinputmultiplexer_15 (
    .BitThree(sixasyncmodcounter_1_output3), .BitTwo(sixasyncmodcounter_1_output2),
    .BitOne(sixasyncmodcounter_1_output1), .Input5(circuitstage6b_1_df1), .Input4(circuitstage6b_1_de1),
    .Input3(circuitstage6b_1_dd1), .Input2(circuitstage6b_1_dc1), .Input1(circuitstage6b_1_db1),
    .InputTimer(circuitstage6b_1_d4), .MultiOut(MINUTES2[3]));

  assign SECOND2[3] = 1'b0;

  // Notes on the sheet:
  //   Minutes
  //   Minutes
  //   Minutes
  //   Minutes
  //   Split Time1
  //   :
  //   Split Time2
  //   :
  //   Split Time3
  //   :
  //   Split Time4
  //   :
  //   Split Time5
  //   Minutes
  //   :
  //   Seconds
  //   Seconds
  //   Seconds
  //   Seconds
  //   Seconds
  //   Minutes
  //   Elapsed Split Time
  //   :
  //   Seconds
endmodule
