// Logisim project stage1.circ as structural Verilog: 1 circuit, main circuit main
module main (
);

  wire button_3_out, t_ff_1_q;

  Button button_1 ();  // open: out
  Button button_2 ();  // open: out
  Button button_3 (.out(button_3_out));
  T_Flip_Flop t_ff_1 (.T(1'b1), .clk(button_3_out), .Q(t_ff_1_q));  // open: Qn, reset, preset
  LED led_1 (.in(t_ff_1_q));
  Hex_Digit_Display hex_digit_display_1 ();  // open: value, dp
  Hex_Digit_Display hex_digit_display_2 ();  // open: value, dp
  Hex_Digit_Display hex_digit_display_3 ();  // open: value, dp
  Hex_Digit_Display hex_digit_display_4 ();  // open: value, dp
  Hex_Digit_Display hex_digit_display_5 ();  // open: value, dp
  Hex_Digit_Display hex_digit_display_6 ();  // open: value, dp
  Hex_Digit_Display hex_digit_display_7 ();  // open: value, dp
  Hex_Digit_Display hex_digit_display_8 ();  // open: value, dp

  // Notes on the sheet:
  //   Split
  //   Reset
  //   Start / Stop
  //   Stopwatch Interface
  //   Register Seconds 01
  //   Minutes
  //   Elapsed Time
  //   :
  //   Seconds
  //   Minutes
  //   Split Time
  //   :
  //   Seconds
endmodule
