// Logisim project stage3.circ as structural Verilog
module main (
);

  wire and_1_out, and_2_out, and_3_out, and_4_out, and_5_out, and_6_out, and_7_out, and_8_out, and_9_out,
       button_2_out, button_3_out, clock_1_out, j_k_ff_1_q, j_k_ff_2_q, j_k_ff_3_q, j_k_ff_4_q, j_k_ff_5_q,
       j_k_ff_6_q, j_k_ff_7_q, or_1_out, or_2_out, t_ff_1_q;
  wire [2:0] d_ff_3_q;
  wire [3:0] d_ff_1_q;

  Button button_1 ();  // open: out
  Button button_2 (.out(button_2_out));
  Button button_3 (.out(button_3_out));
  Clock clock_1 (.out(clock_1_out));
  T_Flip_Flop t_ff_1 (.T(1'b1), .clk(button_3_out), .Q(t_ff_1_q), .reset(button_2_out));  // open: Qn, preset
  and and_1 (and_1_out, clock_1_out, t_ff_1_q);
  J_K_Flip_Flop j_k_ff_1 (
    .J(t_ff_1_q), .K(t_ff_1_q), .clk(clock_1_out), .Q(j_k_ff_1_q), .reset(or_1_out));  // open: Qn, preset
  and and_2 (and_2_out, t_ff_1_q, clock_1_out);
  and and_3 (and_3_out, j_k_ff_2_q, j_k_ff_6_q);
  J_K_Flip_Flop j_k_ff_2 (
    .J(and_4_out), .K(and_4_out), .clk(clock_1_out), .Q(j_k_ff_2_q), .reset(or_1_out));  // open: Qn, preset
  and and_4 (and_4_out, t_ff_1_q, j_k_ff_1_q);
  D_Flip_Flop d_ff_1 (.D(j_k_ff_1_q), .clk(and_2_out), .Q(d_ff_1_q[0]), .reset(button_2_out));  // open: Qn, preset
  J_K_Flip_Flop j_k_ff_3 (
    .J(and_3_out), .K(and_3_out), .clk(and_3_out), .Q(j_k_ff_3_q), .reset(or_2_out));  // open: Qn, preset
  D_Flip_Flop d_ff_2 (.D(j_k_ff_2_q), .clk(and_2_out), .Q(d_ff_1_q[1]), .reset(button_2_out));  // open: Qn, preset
  D_Flip_Flop d_ff_3 (.D(j_k_ff_3_q), .clk(and_1_out), .Q(d_ff_3_q[0]), .reset(button_2_out));  // open: Qn, preset
  and and_5 (and_5_out, and_4_out, j_k_ff_2_q);
  J_K_Flip_Flop j_k_ff_4 (
    .J(and_5_out), .K(and_5_out), .clk(clock_1_out), .Q(j_k_ff_4_q), .reset(or_1_out));  // open: Qn, preset
  J_K_Flip_Flop j_k_ff_5 (
    .J(j_k_ff_3_q), .K(j_k_ff_3_q), .clk(and_3_out), .Q(j_k_ff_5_q), .reset(or_2_out));  // open: Qn, preset
  D_Flip_Flop d_ff_4 (.D(j_k_ff_4_q), .clk(and_2_out), .Q(d_ff_1_q[2]), .reset(button_2_out));  // open: Qn, preset
  and and_6 (and_6_out, j_k_ff_3_q, j_k_ff_5_q);
  D_Flip_Flop d_ff_5 (.D(j_k_ff_5_q), .clk(and_1_out), .Q(d_ff_3_q[1]), .reset(button_2_out));  // open: Qn, preset
  and and_7 (and_7_out, and_5_out, j_k_ff_4_q);
  J_K_Flip_Flop j_k_ff_6 (
    .J(and_7_out), .K(and_7_out), .clk(clock_1_out), .Q(j_k_ff_6_q), .reset(or_1_out));  // open: Qn, preset
  J_K_Flip_Flop j_k_ff_7 (
    .J(and_6_out), .K(and_6_out), .clk(and_3_out), .Q(j_k_ff_7_q), .reset(or_2_out));  // open: Qn, preset
  D_Flip_Flop d_ff_6 (.D(j_k_ff_6_q), .clk(and_2_out), .Q(d_ff_1_q[3]), .reset(button_2_out));  // open: Qn, preset
  D_Flip_Flop d_ff_7 (.D(j_k_ff_7_q), .clk(and_1_out), .Q(d_ff_3_q[2]), .reset(button_2_out));  // open: Qn, preset
  and and_8 (and_8_out, j_k_ff_2_q, j_k_ff_6_q);
  or or_1 (or_1_out, and_8_out, button_2_out);
  and and_9 (and_9_out, j_k_ff_5_q, j_k_ff_7_q);
  or or_2 (or_2_out, and_9_out, button_2_out);
  Hex_Digit_Display hex_digit_display_1 ();  // open: value, dp
  Hex_Digit_Display hex_digit_display_2 ();  // open: value, dp
  Hex_Digit_Display hex_digit_display_3 (.value({1'b0, d_ff_3_q}));  // open: dp
  Hex_Digit_Display hex_digit_display_4 (.value(d_ff_1_q));  // open: dp

  // Notes on the sheet:
  //   Split
  //   Reset
  //   Start / Stop
  //   Stopwatch Interface
  //   Seconds 01
  //   AND gate added to stop count immediately
  //   AND gate to stop count immediately
  //   Seconds 02
  //   Avoids illegal state
  //   OR for reset
  //   OR for reset
  //   Minutes
  //   Elapsed Time
  //   :
  //   Seconds
endmodule
