// Logisim project stage5.circ as structural Verilog: 6 circuits, main circuit main
module main (
);

  wire button_1_out, button_2_out, button_3_out, clock_1_out, fourbitcounter_1_bitfour,
       fourbitcounter_1_bitone, fourbitcounter_1_bitthree, fourbitcounter_1_bittwo, fourbitcounter_1_jkeight,
       fourbitcounter_1_jktwo, fourbitcounter_1_resetout, fourbitcounter_2_bitfour, fourbitcounter_2_bitone,
       fourbitcounter_2_bitthree, fourbitcounter_2_bittwo, threebitcountermodulo6_1_bitone,
       threebitcountermodulo6_1_bitthree, threebitcountermodulo6_1_bittwo, threebitcountermodulo6_1_jkthree,
       threebitcountermodulo6_1_jktwo, threebitcountermodulo6_1_resetout, togglefourbitcounter_1_bitfour,
       togglefourbitcounter_1_bitone, togglefourbitcounter_1_bitthree, togglefourbitcounter_1_bittwo,
       togglefourbitcounter_1_jkeight, togglefourbitcounter_1_jktwo, togglefourbitcounter_1_resetout,
       togglefourbitcounter_1_stopcountimmediateout;
  wire [3:0] fourbitasyncregister_1_hex, fourbitasyncregister_2_hex, fourbitasyncregister_3_hex,
       fourbitcounter_1_hex, fourbitcounter_2_hex, threebitasyncregister_1_hex, threebitcountermodulo6_1_hex,
       togglefourbitcounter_1_hex;

  Button button_1 (.out(button_1_out));
  Button button_2 (.out(button_2_out));
  Button button_3 (.out(button_3_out));
  Clock clock_1 (.out(clock_1_out));
  ToggleFourBitCounter togglefourbitcounter_1 (
    .Reset(button_1_out), .StartStop(button_3_out), .CLK(clock_1_out),
    .ResetOut(togglefourbitcounter_1_resetout), .HEX(togglefourbitcounter_1_hex),
    .StopCountImmediateOut(togglefourbitcounter_1_stopcountimmediateout),
    .JKTwo(togglefourbitcounter_1_jktwo), .JKEight(togglefourbitcounter_1_jkeight),
    .BitOne(togglefourbitcounter_1_bitone), .BitTwo(togglefourbitcounter_1_bittwo),
    .BitThree(togglefourbitcounter_1_bitthree), .BitFour(togglefourbitcounter_1_bitfour));
  FourBitASyncRegister fourbitasyncregister_1 (
    .BitOne(togglefourbitcounter_1_bitone), .BitTwo(togglefourbitcounter_1_bittwo),
    .BitThree(togglefourbitcounter_1_bitthree), .BitFour(togglefourbitcounter_1_bitfour),
    .Reset(button_1_out), .Split(button_2_out), .HEX(fourbitasyncregister_1_hex));  // open: BitFourOut, BitThreeOut, BitTwoOut, BitOneOut
  ThreeBitCounterModulo6 threebitcountermodulo6_1 (
    .Reset(togglefourbitcounter_1_resetout), .IncrementOne(togglefourbitcounter_1_jktwo),
    .IncrementTwo(togglefourbitcounter_1_jkeight), .CLK(clock_1_out),
    .ResetOut(threebitcountermodulo6_1_resetout), .HEX(threebitcountermodulo6_1_hex),
    .JKTwo(threebitcountermodulo6_1_jktwo), .JkThree(threebitcountermodulo6_1_jkthree),
    .BitOne(threebitcountermodulo6_1_bitone), .BitTwo(threebitcountermodulo6_1_bittwo),
    .BitThree(threebitcountermodulo6_1_bitthree));
  ThreeBitASyncRegister threebitasyncregister_1 (
    .BitOne(threebitcountermodulo6_1_bitone), .BitTwo(threebitcountermodulo6_1_bittwo),
    .BitThree(threebitcountermodulo6_1_bitthree), .Reset(button_1_out), .Split(button_2_out),
    .HEX(threebitasyncregister_1_hex));  // open: BitThreeOut, BitTwoOut, BitOneOut
  FourBitCounter fourbitcounter_1 (
    .Reset(threebitcountermodulo6_1_resetout), .IncrementOne(threebitcountermodulo6_1_jktwo),
    .IncrementTwo(threebitcountermodulo6_1_jkthree), .CLK(clock_1_out),
    .StopCountImmediate(togglefourbitcounter_1_stopcountimmediateout), .ResetOut(fourbitcounter_1_resetout),
    .HEX(fourbitcounter_1_hex), .JKTwo(fourbitcounter_1_jktwo), .JKEight(fourbitcounter_1_jkeight),
    .BitOne(fourbitcounter_1_bitone), .BitTwo(fourbitcounter_1_bittwo), .BitThree(fourbitcounter_1_bitthree),
    .BitFour(fourbitcounter_1_bitfour));
  FourBitASyncRegister fourbitasyncregister_2 (
    .BitOne(fourbitcounter_1_bitone), .BitTwo(fourbitcounter_1_bittwo), .BitThree(fourbitcounter_1_bitthree),
    .BitFour(fourbitcounter_1_bitfour), .Reset(button_1_out), .Split(button_2_out),
    .HEX(fourbitasyncregister_2_hex));  // open: BitFourOut, BitThreeOut, BitTwoOut, BitOneOut
  FourBitCounter fourbitcounter_2 (
    .Reset(fourbitcounter_1_resetout), .IncrementOne(fourbitcounter_1_jktwo),
    .IncrementTwo(fourbitcounter_1_jkeight), .CLK(clock_1_out),
    .StopCountImmediate(togglefourbitcounter_1_stopcountimmediateout), .HEX(fourbitcounter_2_hex),
    .BitOne(fourbitcounter_2_bitone), .BitTwo(fourbitcounter_2_bittwo), .BitThree(fourbitcounter_2_bitthree),
    .BitFour(fourbitcounter_2_bitfour));  // open: ResetOut, JKTwo, JKEight
  FourBitASyncRegister fourbitasyncregister_3 (
    .BitOne(fourbitcounter_2_bitone), .BitTwo(fourbitcounter_2_bittwo), .BitThree(fourbitcounter_2_bitthree),
    .BitFour(fourbitcounter_2_bitfour), .Reset(button_1_out), .Split(button_2_out),
    .HEX(fourbitasyncregister_3_hex));  // open: BitFourOut, BitThreeOut, BitTwoOut, BitOneOut
  Hex_Digit_Display hex_digit_display_1 (.value(fourbitcounter_2_hex));  // open: dp
  Hex_Digit_Display hex_digit_display_2 (.value(fourbitasyncregister_3_hex));  // open: dp
  Hex_Digit_Display hex_digit_display_3 (.value(fourbitasyncregister_2_hex));  // open: dp
  Hex_Digit_Display hex_digit_display_4 (.value(fourbitcounter_1_hex));  // open: dp
  Hex_Digit_Display hex_digit_display_5 (.value(threebitasyncregister_1_hex));  // open: dp
  Hex_Digit_Display hex_digit_display_6 (.value(threebitcountermodulo6_1_hex));  // open: dp
  Hex_Digit_Display hex_digit_display_7 (.value(togglefourbitcounter_1_hex));  // open: dp
  Hex_Digit_Display hex_digit_display_8 (.value(fourbitasyncregister_1_hex));  // open: dp

  // Notes on the sheet:
  //   Split
  //   Reset
  //   Stopwatch Interface
  //   Start / Stop
  //   Minutes
  //   Elapsed Time
  //   Minutes
  //   :
  //   Split Time
  //   Seconds
  //   :
  //   Seconds
endmodule

module FourBitCounter (
  input  Reset,
  input  IncrementOne,
  input  IncrementTwo,
  input  CLK,
  input  StopCountImmediate,
  output ResetOut,
  output [3:0] HEX,
  output JKTwo,
  output JKEight,
  output BitOne,
  output BitTwo,
  output BitThree,
  output BitFour
);

  wire and_1_out, and_2_out, and_3_out, and_4_out, and_5_out, and_6_out, j_k_ff_1_q, j_k_ff_3_q, or_1_out;

  and and_1 (and_1_out, IncrementOne, IncrementTwo);
  J_K_Flip_Flop j_k_ff_1 (
    .J(and_1_out), .K(and_1_out), .clk(and_1_out), .Q(j_k_ff_1_q), .reset(or_1_out));  // open: Qn, preset
  and and_2 (and_2_out, CLK, StopCountImmediate);
  D_Flip_Flop d_ff_1 (.D(j_k_ff_1_q), .clk(and_2_out), .Q(BitOne), .reset(Reset));  // open: Qn, preset
  J_K_Flip_Flop j_k_ff_2 (
    .J(and_3_out), .K(and_3_out), .clk(and_1_out), .Q(JKTwo), .reset(or_1_out));  // open: Qn, preset
  buf and_3 (and_3_out, j_k_ff_1_q);  // AND_Gate
  and and_4 (and_4_out, and_3_out, JKTwo);
  D_Flip_Flop d_ff_2 (.D(JKTwo), .clk(and_2_out), .Q(BitTwo), .reset(Reset));  // open: Qn, preset
  J_K_Flip_Flop j_k_ff_3 (
    .J(and_4_out), .K(and_4_out), .clk(and_1_out), .Q(j_k_ff_3_q), .reset(or_1_out));  // open: Qn, preset
  and and_5 (and_5_out, and_4_out, j_k_ff_3_q);
  J_K_Flip_Flop j_k_ff_4 (
    .J(and_5_out), .K(and_5_out), .clk(and_1_out), .Q(JKEight), .reset(or_1_out));  // open: Qn, preset
  D_Flip_Flop d_ff_3 (.D(j_k_ff_3_q), .clk(and_2_out), .Q(BitThree), .reset(Reset));  // open: Qn, preset
  and and_6 (and_6_out, JKTwo, JKEight);
  or or_1 (or_1_out, and_6_out, Reset);
  D_Flip_Flop d_ff_4 (.D(JKEight), .clk(and_2_out), .Q(BitFour), .reset(Reset));  // open: Qn, preset

  assign HEX = {BitFour, BitThree, BitTwo, BitOne};
  assign ResetOut = Reset;

  // Notes on the sheet:
  //   Avoids illegal state
  //   OR for reset
endmodule

module ToggleFourBitCounter (
  input  Reset,
  input  StartStop,
  input  CLK,
  output ResetOut,
  output [3:0] HEX,
  output StopCountImmediateOut,
  output JKTwo,
  output JKEight,
  output BitOne,
  output BitTwo,
  output BitThree,
  output BitFour
);

  wire and_1_out, and_2_out, and_3_out, and_4_out, and_5_out, j_k_ff_1_q, j_k_ff_3_q, or_1_out;

  T_Flip_Flop t_ff_1 (.T(1'b1), .clk(StartStop), .Q(StopCountImmediateOut), .reset(Reset));  // open: Qn, preset
  J_K_Flip_Flop j_k_ff_1 (
    .J(StopCountImmediateOut), .K(StopCountImmediateOut), .clk(CLK), .Q(j_k_ff_1_q), .reset(or_1_out));  // open: Qn, preset
  and and_1 (and_1_out, StopCountImmediateOut, CLK);
  D_Flip_Flop d_ff_1 (.D(j_k_ff_1_q), .clk(and_1_out), .Q(BitOne), .reset(Reset));  // open: Qn, preset
  J_K_Flip_Flop j_k_ff_2 (.J(and_2_out), .K(and_2_out), .clk(CLK), .Q(JKTwo), .reset(or_1_out));  // open: Qn, preset
  and and_2 (and_2_out, StopCountImmediateOut, j_k_ff_1_q);
  D_Flip_Flop d_ff_2 (.D(JKTwo), .clk(and_1_out), .Q(BitTwo), .reset(Reset));  // open: Qn, preset
  and and_3 (and_3_out, and_2_out, JKTwo);
  J_K_Flip_Flop j_k_ff_3 (
    .J(and_3_out), .K(and_3_out), .clk(CLK), .Q(j_k_ff_3_q), .reset(or_1_out));  // open: Qn, preset
  and and_4 (and_4_out, and_3_out, j_k_ff_3_q);
  D_Flip_Flop d_ff_3 (.D(j_k_ff_3_q), .clk(and_1_out), .Q(BitThree), .reset(Reset));  // open: Qn, preset
  J_K_Flip_Flop j_k_ff_4 (.J(and_4_out), .K(and_4_out), .clk(CLK), .Q(JKEight), .reset(or_1_out));  // open: Qn, preset
  and and_5 (and_5_out, JKTwo, JKEight);
  or or_1 (or_1_out, and_5_out, Reset);
  D_Flip_Flop d_ff_4 (.D(JKEight), .clk(and_1_out), .Q(BitFour), .reset(Reset));  // open: Qn, preset

  assign HEX = {BitFour, BitThree, BitTwo, BitOne};
  assign ResetOut = Reset;

  // Notes on the sheet:
  //   Avoids illegal state
  //   OR for reset
endmodule

module ThreeBitCounterModulo6 (
  input  Reset,
  input  IncrementOne,
  input  IncrementTwo,
  input  CLK,
  output ResetOut,
  output [3:0] HEX,
  output JKTwo,
  output JkThree,
  output BitOne,
  output BitTwo,
  output BitThree
);

  wire and_1_out, and_2_out, and_3_out, j_k_ff_1_q, or_1_out;

  and and_1 (and_1_out, IncrementOne, IncrementTwo);
  J_K_Flip_Flop j_k_ff_1 (
    .J(and_1_out), .K(and_1_out), .clk(and_1_out), .Q(j_k_ff_1_q), .reset(or_1_out));  // open: Qn, preset
  D_Flip_Flop d_ff_1 (.D(j_k_ff_1_q), .clk(CLK), .Q(BitOne), .reset(Reset));  // open: Qn, preset
  J_K_Flip_Flop j_k_ff_2 (
    .J(j_k_ff_1_q), .K(j_k_ff_1_q), .clk(and_1_out), .Q(JKTwo), .reset(or_1_out));  // open: Qn, preset
  D_Flip_Flop d_ff_2 (.D(JKTwo), .clk(CLK), .Q(BitTwo), .reset(Reset));  // open: Qn, preset
  J_K_Flip_Flop j_k_ff_3 (
    .J(and_2_out), .K(and_2_out), .clk(and_1_out), .Q(JkThree), .reset(or_1_out));  // open: Qn, preset
  and and_2 (and_2_out, j_k_ff_1_q, JKTwo);
  D_Flip_Flop d_ff_3 (.D(JkThree), .clk(CLK), .Q(BitThree), .reset(Reset));  // open: Qn, preset
  and and_3 (and_3_out, JKTwo, JkThree);
  or or_1 (or_1_out, and_3_out, Reset);

  assign HEX = {1'b0, BitThree, BitTwo, BitOne};
  assign ResetOut = Reset;

  // Notes on the sheet:
  //   Seconds 02
  //   OR for reset
endmodule

module FourBitASyncRegister (
  input  BitOne,
  input  BitTwo,
  input  BitThree,
  input  BitFour,
  input  Reset,
  input  Split,
  output BitFourOut,
  output BitThreeOut,
  output BitTwoOut,
  output BitOneOut,
  output [3:0] HEX
);

  D_Flip_Flop d_ff_1 (.D(BitOne), .clk(Split), .Q(BitOneOut), .reset(Reset));  // open: Qn, preset
  D_Flip_Flop d_ff_2 (.D(BitTwo), .clk(Split), .Q(BitTwoOut), .reset(Reset));  // open: Qn, preset
  D_Flip_Flop d_ff_3 (.D(BitThree), .clk(Split), .Q(BitThreeOut), .reset(Reset));  // open: Qn, preset
  D_Flip_Flop d_ff_4 (.D(BitFour), .clk(Split), .Q(BitFourOut), .reset(Reset));  // open: Qn, preset

  assign HEX = {BitFourOut, BitThreeOut, BitTwoOut, BitOneOut};
endmodule

module ThreeBitASyncRegister (
  input  BitOne,
  input  BitTwo,
  input  BitThree,
  input  Reset,
  input  Split,
  output BitThreeOut,
  output BitTwoOut,
  output BitOneOut,
  output [3:0] HEX
);

  D_Flip_Flop d_ff_1 (.D(BitOne), .clk(Split), .Q(BitOneOut), .reset(Reset));  // open: Qn, preset
  D_Flip_Flop d_ff_2 (.D(BitTwo), .clk(Split), .Q(BitTwoOut), .reset(Reset));  // open: Qn, preset
  D_Flip_Flop d_ff_3 (.D(BitThree), .clk(Split), .Q(BitThreeOut), .reset(Reset));  // open: Qn, preset

  assign HEX = {1'b0, BitThreeOut, BitTwoOut, BitOneOut};
endmodule
