// Logisim project stage6a.circ as structural Verilog: 6 circuits, main circuit main
module main (
);

  wire button_1_out, button_2_out, button_3_out, clock_1_out, fourbitasyncregister_1_bitfourout,
       fourbitasyncregister_1_bitoneout, fourbitasyncregister_1_bitthreeout,
       fourbitasyncregister_1_bittwoout, fourbitasyncregister_2_bitfourout, fourbitasyncregister_2_bitoneout,
       fourbitasyncregister_2_bitthreeout, fourbitasyncregister_2_bittwoout,
       fourbitasyncregister_3_bitfourout, fourbitasyncregister_3_bitoneout,
       fourbitasyncregister_3_bitthreeout, fourbitasyncregister_3_bittwoout,
       fourbitasyncregister_4_bitfourout, fourbitasyncregister_4_bitoneout,
       fourbitasyncregister_4_bitthreeout, fourbitasyncregister_4_bittwoout,
       fourbitasyncregister_5_bitfourout, fourbitasyncregister_5_bitoneout,
       fourbitasyncregister_5_bitthreeout, fourbitasyncregister_5_bittwoout,
       fourbitasyncregister_6_bitfourout, fourbitasyncregister_6_bitoneout,
       fourbitasyncregister_6_bitthreeout, fourbitasyncregister_6_bittwoout,
       fourbitasyncregister_8_bitfourout, fourbitasyncregister_8_bitoneout,
       fourbitasyncregister_8_bitthreeout, fourbitasyncregister_8_bittwoout,
       fourbitasyncregister_9_bitfourout, fourbitasyncregister_9_bitoneout,
       fourbitasyncregister_9_bitthreeout, fourbitasyncregister_9_bittwoout,
       fourbitasyncregister_10_bitfourout, fourbitasyncregister_10_bitoneout,
       fourbitasyncregister_10_bitthreeout, fourbitasyncregister_10_bittwoout,
       fourbitasyncregister_11_bitfourout, fourbitasyncregister_11_bitoneout,
       fourbitasyncregister_11_bitthreeout, fourbitasyncregister_11_bittwoout,
       fourbitasyncregister_12_bitfourout, fourbitasyncregister_12_bitoneout,
       fourbitasyncregister_12_bitthreeout, fourbitasyncregister_12_bittwoout,
       fourbitasyncregister_14_bitfourout, fourbitasyncregister_14_bitoneout,
       fourbitasyncregister_14_bitthreeout, fourbitasyncregister_14_bittwoout, fourbitcounter_1_bitfour,
       fourbitcounter_1_bitone, fourbitcounter_1_bitthree, fourbitcounter_1_bittwo, fourbitcounter_1_jkeight,
       fourbitcounter_1_jktwo, fourbitcounter_1_resetout, fourbitcounter_2_bitfour, fourbitcounter_2_bitone,
       fourbitcounter_2_bitthree, fourbitcounter_2_bittwo, nand_1_out, nand_2_out, not_1_out, not_2_out,
       threebitasyncregister_1_bitoneout, threebitasyncregister_1_bitthreeout,
       threebitasyncregister_1_bittwoout, threebitasyncregister_2_bitoneout,
       threebitasyncregister_2_bitthreeout, threebitasyncregister_2_bittwoout,
       threebitasyncregister_3_bitoneout, threebitasyncregister_3_bitthreeout,
       threebitasyncregister_3_bittwoout, threebitasyncregister_4_bitoneout,
       threebitasyncregister_4_bitthreeout, threebitasyncregister_4_bittwoout,
       threebitcountermodulo6_1_bitone, threebitcountermodulo6_1_bitthree, threebitcountermodulo6_1_bittwo,
       threebitcountermodulo6_1_jkthree, threebitcountermodulo6_1_jktwo, threebitcountermodulo6_1_resetout,
       togglefourbitcounter_1_bitfour, togglefourbitcounter_1_bitone, togglefourbitcounter_1_bitthree,
       togglefourbitcounter_1_bittwo, togglefourbitcounter_1_jkeight, togglefourbitcounter_1_jktwo,
       togglefourbitcounter_1_resetout, togglefourbitcounter_1_stopcountimmediateout;
  wire [3:0] fourbitasyncregister_1_hex, fourbitasyncregister_2_hex, fourbitasyncregister_3_hex,
       fourbitasyncregister_4_hex, fourbitasyncregister_5_hex, fourbitasyncregister_6_hex,
       fourbitasyncregister_7_hex, fourbitasyncregister_8_hex, fourbitasyncregister_9_hex,
       fourbitasyncregister_10_hex, fourbitasyncregister_11_hex, fourbitasyncregister_12_hex,
       fourbitasyncregister_13_hex, fourbitasyncregister_14_hex, fourbitasyncregister_15_hex,
       fourbitcounter_1_hex, fourbitcounter_2_hex, threebitasyncregister_1_hex, threebitasyncregister_2_hex,
       threebitasyncregister_3_hex, threebitasyncregister_4_hex, threebitasyncregister_5_hex,
       threebitcountermodulo6_1_hex, togglefourbitcounter_1_hex;

  nand nand_1 (nand_1_out, button_3_out, nand_2_out);
  not not_1 (not_1_out, nand_1_out);
  nand nand_2 (nand_2_out, nand_1_out, not_2_out);
  Clock clock_1 (.out(clock_1_out));
  not not_2 (not_2_out, togglefourbitcounter_1_stopcountimmediateout);
  ToggleFourBitCounter togglefourbitcounter_1 (
    .Reset(button_1_out), .StartStop(button_2_out), .CLK(clock_1_out),
    .ResetOut(togglefourbitcounter_1_resetout), .HEX(togglefourbitcounter_1_hex),
    .StopCountImmediateOut(togglefourbitcounter_1_stopcountimmediateout),
    .JKTwo(togglefourbitcounter_1_jktwo), .JKEight(togglefourbitcounter_1_jkeight),
    .BitOne(togglefourbitcounter_1_bitone), .BitTwo(togglefourbitcounter_1_bittwo),
    .BitThree(togglefourbitcounter_1_bitthree), .BitFour(togglefourbitcounter_1_bitfour));
  FourBitASyncRegister fourbitasyncregister_1 (
    .BitOne(togglefourbitcounter_1_bitone), .BitTwo(togglefourbitcounter_1_bittwo),
    .BitThree(togglefourbitcounter_1_bitthree), .BitFour(togglefourbitcounter_1_bitfour),
    .Reset(button_1_out), .Split(not_1_out), .BitFourOut(fourbitasyncregister_1_bitfourout),
    .BitThreeOut(fourbitasyncregister_1_bitthreeout), .BitTwoOut(fourbitasyncregister_1_bittwoout),
    .BitOneOut(fourbitasyncregister_1_bitoneout), .HEX(fourbitasyncregister_1_hex));
  FourBitASyncRegister fourbitasyncregister_2 (
    .BitOne(fourbitasyncregister_1_bitoneout), .BitTwo(fourbitasyncregister_1_bittwoout),
    .BitThree(fourbitasyncregister_1_bitthreeout), .BitFour(fourbitasyncregister_1_bitfourout),
    .Reset(button_1_out), .Split(not_1_out), .BitFourOut(fourbitasyncregister_2_bitfourout),
    .BitThreeOut(fourbitasyncregister_2_bitthreeout), .BitTwoOut(fourbitasyncregister_2_bittwoout),
    .BitOneOut(fourbitasyncregister_2_bitoneout), .HEX(fourbitasyncregister_2_hex));
  ThreeBitCounterModulo6 threebitcountermodulo6_1 (
    .Reset(togglefourbitcounter_1_resetout), .IncrementOne(togglefourbitcounter_1_jktwo),
    .IncrementTwo(togglefourbitcounter_1_jkeight), .CLK(clock_1_out),
    .ResetOut(threebitcountermodulo6_1_resetout), .HEX(threebitcountermodulo6_1_hex),
    .JKTwo(threebitcountermodulo6_1_jktwo), .JkThree(threebitcountermodulo6_1_jkthree),
    .BitOne(threebitcountermodulo6_1_bitone), .BitTwo(threebitcountermodulo6_1_bittwo),
    .BitThree(threebitcountermodulo6_1_bitthree));
  ThreeBitASyncRegister threebitasyncregister_1 (
    .BitOne(threebitcountermodulo6_1_bitone), .BitTwo(threebitcountermodulo6_1_bittwo),
    .BitThree(threebitcountermodulo6_1_bitthree), .Reset(button_1_out), .Split(not_1_out),
    .BitThreeOut(threebitasyncregister_1_bitthreeout), .BitTwoOut(threebitasyncregister_1_bittwoout),
    .BitOneOut(threebitasyncregister_1_bitoneout), .HEX(threebitasyncregister_1_hex));
  FourBitASyncRegister fourbitasyncregister_3 (
    .BitOne(fourbitasyncregister_2_bitoneout), .BitTwo(fourbitasyncregister_2_bittwoout),
    .BitThree(fourbitasyncregister_2_bitthreeout), .BitFour(fourbitasyncregister_2_bitfourout),
    .Reset(button_1_out), .Split(not_1_out), .BitFourOut(fourbitasyncregister_3_bitfourout),
    .BitThreeOut(fourbitasyncregister_3_bitthreeout), .BitTwoOut(fourbitasyncregister_3_bittwoout),
    .BitOneOut(fourbitasyncregister_3_bitoneout), .HEX(fourbitasyncregister_3_hex));
  ThreeBitASyncRegister threebitasyncregister_2 (
    .BitOne(threebitasyncregister_1_bitoneout), .BitTwo(threebitasyncregister_1_bittwoout),
    .BitThree(threebitasyncregister_1_bitthreeout), .Reset(button_1_out), .Split(not_1_out),
    .BitThreeOut(threebitasyncregister_2_bitthreeout), .BitTwoOut(threebitasyncregister_2_bittwoout),
    .BitOneOut(threebitasyncregister_2_bitoneout), .HEX(threebitasyncregister_2_hex));
  FourBitCounter fourbitcounter_1 (
    .Reset(threebitcountermodulo6_1_resetout), .IncrementOne(threebitcountermodulo6_1_jktwo),
    .IncrementTwo(threebitcountermodulo6_1_jkthree), .CLK(clock_1_out),
    .StopCountImmediate(togglefourbitcounter_1_stopcountimmediateout), .ResetOut(fourbitcounter_1_resetout),
    .HEX(fourbitcounter_1_hex), .JKTwo(fourbitcounter_1_jktwo), .JKEight(fourbitcounter_1_jkeight),
    .BitOne(fourbitcounter_1_bitone), .BitTwo(fourbitcounter_1_bittwo), .BitThree(fourbitcounter_1_bitthree),
    .BitFour(fourbitcounter_1_bitfour));
  FourBitASyncRegister fourbitasyncregister_4 (
    .BitOne(fourbitcounter_1_bitone), .BitTwo(fourbitcounter_1_bittwo), .BitThree(fourbitcounter_1_bitthree),
    .BitFour(fourbitcounter_1_bitfour), .Reset(button_1_out), .Split(not_1_out),
    .BitFourOut(fourbitasyncregister_4_bitfourout), .BitThreeOut(fourbitasyncregister_4_bitthreeout),
    .BitTwoOut(fourbitasyncregister_4_bittwoout), .BitOneOut(fourbitasyncregister_4_bitoneout),
    .HEX(fourbitasyncregister_4_hex));
  FourBitASyncRegister fourbitasyncregister_5 (
    .BitOne(fourbitasyncregister_3_bitoneout), .BitTwo(fourbitasyncregister_3_bittwoout),
    .BitThree(fourbitasyncregister_3_bitthreeout), .BitFour(fourbitasyncregister_3_bitfourout),
    .Reset(button_1_out), .Split(not_1_out), .BitFourOut(fourbitasyncregister_5_bitfourout),
    .BitThreeOut(fourbitasyncregister_5_bitthreeout), .BitTwoOut(fourbitasyncregister_5_bittwoout),
    .BitOneOut(fourbitasyncregister_5_bitoneout), .HEX(fourbitasyncregister_5_hex));
  ThreeBitASyncRegister threebitasyncregister_3 (
    .BitOne(threebitasyncregister_2_bitoneout), .BitTwo(threebitasyncregister_2_bittwoout),
    .BitThree(threebitasyncregister_2_bitthreeout), .Reset(button_1_out), .Split(not_1_out),
    .BitThreeOut(threebitasyncregister_3_bitthreeout), .BitTwoOut(threebitasyncregister_3_bittwoout),
    .BitOneOut(threebitasyncregister_3_bitoneout), .HEX(threebitasyncregister_3_hex));
  FourBitASyncRegister fourbitasyncregister_6 (
    .BitOne(fourbitasyncregister_4_bitoneout), .BitTwo(fourbitasyncregister_4_bittwoout),
    .BitThree(fourbitasyncregister_4_bitthreeout), .BitFour(fourbitasyncregister_4_bitfourout),
    .Reset(button_1_out), .Split(not_1_out), .BitFourOut(fourbitasyncregister_6_bitfourout),
    .BitThreeOut(fourbitasyncregister_6_bitthreeout), .BitTwoOut(fourbitasyncregister_6_bittwoout),
    .BitOneOut(fourbitasyncregister_6_bitoneout), .HEX(fourbitasyncregister_6_hex));
  FourBitASyncRegister fourbitasyncregister_7 (
    .BitOne(fourbitasyncregister_5_bitoneout), .BitTwo(fourbitasyncregister_5_bittwoout),
    .BitThree(fourbitasyncregister_5_bitthreeout), .BitFour(fourbitasyncregister_5_bitfourout),
    .Reset(button_1_out), .Split(not_1_out), .HEX(fourbitasyncregister_7_hex));  // open: BitFourOut, BitThreeOut, BitTwoOut, BitOneOut
  FourBitCounter fourbitcounter_2 (
    .Reset(fourbitcounter_1_resetout), .IncrementOne(fourbitcounter_1_jktwo),
    .IncrementTwo(fourbitcounter_1_jkeight), .CLK(clock_1_out),
    .StopCountImmediate(togglefourbitcounter_1_stopcountimmediateout), .HEX(fourbitcounter_2_hex),
    .BitOne(fourbitcounter_2_bitone), .BitTwo(fourbitcounter_2_bittwo), .BitThree(fourbitcounter_2_bitthree),
    .BitFour(fourbitcounter_2_bitfour));  // open: ResetOut, JKTwo, JKEight
  FourBitASyncRegister fourbitasyncregister_8 (
    .BitOne(fourbitcounter_2_bitone), .BitTwo(fourbitcounter_2_bittwo), .BitThree(fourbitcounter_2_bitthree),
    .BitFour(fourbitcounter_2_bitfour), .Reset(button_1_out), .Split(not_1_out),
    .BitFourOut(fourbitasyncregister_8_bitfourout), .BitThreeOut(fourbitasyncregister_8_bitthreeout),
    .BitTwoOut(fourbitasyncregister_8_bittwoout), .BitOneOut(fourbitasyncregister_8_bitoneout),
    .HEX(fourbitasyncregister_8_hex));
  ThreeBitASyncRegister threebitasyncregister_4 (
    .BitOne(threebitasyncregister_3_bitoneout), .BitTwo(threebitasyncregister_3_bittwoout),
    .BitThree(threebitasyncregister_3_bitthreeout), .Reset(button_1_out), .Split(not_1_out),
    .BitThreeOut(threebitasyncregister_4_bitthreeout), .BitTwoOut(threebitasyncregister_4_bittwoout),
    .BitOneOut(threebitasyncregister_4_bitoneout), .HEX(threebitasyncregister_4_hex));
  Button button_1 (.out(button_1_out));
  Button button_2 (.out(button_2_out));
  Button button_3 (.out(button_3_out));
  Hex_Digit_Display hex_digit_display_1 (.value(fourbitasyncregister_8_hex));  // open: dp
  Hex_Digit_Display hex_digit_display_2 (.value(fourbitcounter_2_hex));  // open: dp
  Hex_Digit_Display hex_digit_display_3 (.value(fourbitcounter_1_hex));  // open: dp
  Hex_Digit_Display hex_digit_display_4 (.value(fourbitasyncregister_4_hex));  // open: dp
  FourBitASyncRegister fourbitasyncregister_9 (
    .BitOne(fourbitasyncregister_6_bitoneout), .BitTwo(fourbitasyncregister_6_bittwoout),
    .BitThree(fourbitasyncregister_6_bitthreeout), .BitFour(fourbitasyncregister_6_bitfourout),
    .Reset(button_1_out), .Split(not_1_out), .BitFourOut(fourbitasyncregister_9_bitfourout),
    .BitThreeOut(fourbitasyncregister_9_bitthreeout), .BitTwoOut(fourbitasyncregister_9_bittwoout),
    .BitOneOut(fourbitasyncregister_9_bitoneout), .HEX(fourbitasyncregister_9_hex));
  Hex_Digit_Display hex_digit_display_5 (.value(threebitcountermodulo6_1_hex));  // open: dp
  Hex_Digit_Display hex_digit_display_6 (.value(threebitasyncregister_1_hex));  // open: dp
  Hex_Digit_Display hex_digit_display_7 (.value(fourbitasyncregister_1_hex));  // open: dp
  FourBitASyncRegister fourbitasyncregister_10 (
    .BitOne(fourbitasyncregister_8_bitoneout), .BitTwo(fourbitasyncregister_8_bittwoout),
    .BitThree(fourbitasyncregister_8_bitthreeout), .BitFour(fourbitasyncregister_8_bitfourout),
    .Reset(button_1_out), .Split(not_1_out), .BitFourOut(fourbitasyncregister_10_bitfourout),
    .BitThreeOut(fourbitasyncregister_10_bitthreeout), .BitTwoOut(fourbitasyncregister_10_bittwoout),
    .BitOneOut(fourbitasyncregister_10_bitoneout), .HEX(fourbitasyncregister_10_hex));
  Hex_Digit_Display hex_digit_display_8 (.value(togglefourbitcounter_1_hex));  // open: dp
  Hex_Digit_Display hex_digit_display_9 (.value(fourbitasyncregister_10_hex));  // open: dp
  ThreeBitASyncRegister threebitasyncregister_5 (
    .BitOne(threebitasyncregister_4_bitoneout), .BitTwo(threebitasyncregister_4_bittwoout),
    .BitThree(threebitasyncregister_4_bitthreeout), .Reset(button_1_out), .Split(not_1_out),
    .HEX(threebitasyncregister_5_hex));  // open: BitThreeOut, BitTwoOut, BitOneOut
  Hex_Digit_Display hex_digit_display_10 (.value(fourbitasyncregister_6_hex));  // open: dp
  FourBitASyncRegister fourbitasyncregister_11 (
    .BitOne(fourbitasyncregister_9_bitoneout), .BitTwo(fourbitasyncregister_9_bittwoout),
    .BitThree(fourbitasyncregister_9_bitthreeout), .BitFour(fourbitasyncregister_9_bitfourout),
    .Reset(button_1_out), .Split(not_1_out), .BitFourOut(fourbitasyncregister_11_bitfourout),
    .BitThreeOut(fourbitasyncregister_11_bitthreeout), .BitTwoOut(fourbitasyncregister_11_bittwoout),
    .BitOneOut(fourbitasyncregister_11_bitoneout), .HEX(fourbitasyncregister_11_hex));
  Hex_Digit_Display hex_digit_display_11 (.value(threebitasyncregister_2_hex));  // open: dp
  Hex_Digit_Display hex_digit_display_12 (.value(fourbitasyncregister_2_hex));  // open: dp
  FourBitASyncRegister fourbitasyncregister_12 (
    .BitOne(fourbitasyncregister_10_bitoneout), .BitTwo(fourbitasyncregister_10_bittwoout),
    .BitThree(fourbitasyncregister_10_bitthreeout), .BitFour(fourbitasyncregister_10_bitfourout),
    .Reset(button_1_out), .Split(not_1_out), .BitFourOut(fourbitasyncregister_12_bitfourout),
    .BitThreeOut(fourbitasyncregister_12_bitthreeout), .BitTwoOut(fourbitasyncregister_12_bittwoout),
    .BitOneOut(fourbitasyncregister_12_bitoneout), .HEX(fourbitasyncregister_12_hex));
  Hex_Digit_Display hex_digit_display_13 (.value(fourbitasyncregister_12_hex));  // open: dp
  Hex_Digit_Display hex_digit_display_14 (.value(fourbitasyncregister_9_hex));  // open: dp
  Hex_Digit_Display hex_digit_display_15 (.value(threebitasyncregister_3_hex));  // open: dp
  FourBitASyncRegister fourbitasyncregister_13 (
    .BitOne(fourbitasyncregister_11_bitoneout), .BitTwo(fourbitasyncregister_11_bittwoout),
    .BitThree(fourbitasyncregister_11_bitthreeout), .BitFour(fourbitasyncregister_11_bitfourout),
    .Reset(button_1_out), .Split(not_1_out), .HEX(fourbitasyncregister_13_hex));  // open: BitFourOut, BitThreeOut, BitTwoOut, BitOneOut
  Hex_Digit_Display hex_digit_display_16 (.value(fourbitasyncregister_3_hex));  // open: dp
  FourBitASyncRegister fourbitasyncregister_14 (
    .BitOne(fourbitasyncregister_12_bitoneout), .BitTwo(fourbitasyncregister_12_bittwoout),
    .BitThree(fourbitasyncregister_12_bitthreeout), .BitFour(fourbitasyncregister_12_bitfourout),
    .Reset(button_1_out), .Split(not_1_out), .BitFourOut(fourbitasyncregister_14_bitfourout),
    .BitThreeOut(fourbitasyncregister_14_bitthreeout), .BitTwoOut(fourbitasyncregister_14_bittwoout),
    .BitOneOut(fourbitasyncregister_14_bitoneout), .HEX(fourbitasyncregister_14_hex));
  Hex_Digit_Display hex_digit_display_17 (.value(fourbitasyncregister_14_hex));  // open: dp
  Hex_Digit_Display hex_digit_display_18 (.value(fourbitasyncregister_11_hex));  // open: dp
  Hex_Digit_Display hex_digit_display_19 (.value(threebitasyncregister_4_hex));  // open: dp
  Hex_Digit_Display hex_digit_display_20 (.value(fourbitasyncregister_5_hex));  // open: dp
  Hex_Digit_Display hex_digit_display_21 (.value(fourbitasyncregister_15_hex));  // open: dp
  FourBitASyncRegister fourbitasyncregister_15 (
    .BitOne(fourbitasyncregister_14_bitoneout), .BitTwo(fourbitasyncregister_14_bittwoout),
    .BitThree(fourbitasyncregister_14_bitthreeout), .BitFour(fourbitasyncregister_14_bitfourout),
    .Reset(button_1_out), .Split(not_1_out), .HEX(fourbitasyncregister_15_hex));  // open: BitFourOut, BitThreeOut, BitTwoOut, BitOneOut
  Hex_Digit_Display hex_digit_display_22 (.value(fourbitasyncregister_13_hex));  // open: dp
  Hex_Digit_Display hex_digit_display_23 (.value(threebitasyncregister_5_hex));  // open: dp
  Hex_Digit_Display hex_digit_display_24 (.value(fourbitasyncregister_7_hex));  // open: dp

  // Notes on the sheet:
  //   Stopwatch Interface
  //   Reset
  //   Start / Stop
  //   Split
  //   Minutes
  //   Minutes
  //   Split Time
  //   :
  //   Elapsed Time
  //   :
  //   Seconds
  //   Seconds
  //   Split Time 2
  //   Minutes
  //   :
  //   Seconds
  //   Minutes
  //   Split Time 3
  //   Seconds
  //   :
  //   Split Time 4
  //   Minutes
  //   :
  //   Seconds
  //   Split Time 5
  //   Minutes
  //   :
  //   Seconds
endmodule

module FourBitCounter (
  input  Reset,
  input  IncrementOne,
  input  IncrementTwo,
  input  CLK,
  input  StopCountImmediate,
  output ResetOut,
  output [3:0] HEX,
  output JKTwo,
  output JKEight,
  output BitOne,
  output BitTwo,
  output BitThree,
  output BitFour
);

  wire and_1_out, and_2_out, and_3_out, and_4_out, and_5_out, and_6_out, j_k_ff_1_q, j_k_ff_3_q, or_1_out;

  and and_1 (and_1_out, IncrementOne, IncrementTwo);
  J_K_Flip_Flop j_k_ff_1 (
    .J(and_1_out), .K(and_1_out), .clk(and_1_out), .Q(j_k_ff_1_q), .reset(or_1_out));  // open: Qn, preset
  and and_2 (and_2_out, CLK, StopCountImmediate);
  D_Flip_Flop d_ff_1 (.D(j_k_ff_1_q), .clk(and_2_out), .Q(BitOne), .reset(Reset));  // open: Qn, preset
  J_K_Flip_Flop j_k_ff_2 (
    .J(and_3_out), .K(and_3_out), .clk(and_1_out), .Q(JKTwo), .reset(or_1_out));  // open: Qn, preset
  buf and_3 (and_3_out, j_k_ff_1_q);  // AND_Gate
  and and_4 (and_4_out, and_3_out, JKTwo);
  D_Flip_Flop d_ff_2 (.D(JKTwo), .clk(and_2_out), .Q(BitTwo), .reset(Reset));  // open: Qn, preset
  J_K_Flip_Flop j_k_ff_3 (
    .J(and_4_out), .K(and_4_out), .clk(and_1_out), .Q(j_k_ff_3_q), .reset(or_1_out));  // open: Qn, preset
  and and_5 (and_5_out, and_4_out, j_k_ff_3_q);
  J_K_Flip_Flop j_k_ff_4 (
    .J(and_5_out), .K(and_5_out), .clk(and_1_out), .Q(JKEight), .reset(or_1_out));  // open: Qn, preset
  D_Flip_Flop d_ff_3 (.D(j_k_ff_3_q), .clk(and_2_out), .Q(BitThree), .reset(Reset));  // open: Qn, preset
  and and_6 (and_6_out, JKTwo, JKEight);
  or or_1 (or_1_out, and_6_out, Reset);
  D_Flip_Flop d_ff_4 (.D(JKEight), .clk(and_2_out), .Q(BitFour), .reset(Reset));  // open: Qn, preset

  assign HEX = {BitFour, BitThree, BitTwo, BitOne};
  assign ResetOut = Reset;

  // Notes on the sheet:
  //   Avoids illegal state
  //   OR for reset
endmodule

module ToggleFourBitCounter (
  input  Reset,
  input  StartStop,
  input  CLK,
  output ResetOut,
  output [3:0] HEX,
  output StopCountImmediateOut,
  output JKTwo,
  output JKEight,
  output BitOne,
  output BitTwo,
  output BitThree,
  output BitFour
);

  wire and_1_out, and_2_out, and_3_out, and_4_out, and_5_out, j_k_ff_1_q, j_k_ff_3_q, or_1_out;

  T_Flip_Flop t_ff_1 (.T(1'b1), .clk(StartStop), .Q(StopCountImmediateOut), .reset(Reset));  // open: Qn, preset
  J_K_Flip_Flop j_k_ff_1 (
    .J(StopCountImmediateOut), .K(StopCountImmediateOut), .clk(CLK), .Q(j_k_ff_1_q), .reset(or_1_out));  // open: Qn, preset
  and and_1 (and_1_out, StopCountImmediateOut, CLK);
  D_Flip_Flop d_ff_1 (.D(j_k_ff_1_q), .clk(and_1_out), .Q(BitOne), .reset(Reset));  // open: Qn, preset
  J_K_Flip_Flop j_k_ff_2 (.J(and_2_out), .K(and_2_out), .clk(CLK), .Q(JKTwo), .reset(or_1_out));  // open: Qn, preset
  and and_2 (and_2_out, StopCountImmediateOut, j_k_ff_1_q);
  D_Flip_Flop d_ff_2 (.D(JKTwo), .clk(and_1_out), .Q(BitTwo), .reset(Reset));  // open: Qn, preset
  and and_3 (and_3_out, and_2_out, JKTwo);
  J_K_Flip_Flop j_k_ff_3 (
    .J(and_3_out), .K(and_3_out), .clk(CLK), .Q(j_k_ff_3_q), .reset(or_1_out));  // open: Qn, preset
  and and_4 (and_4_out, and_3_out, j_k_ff_3_q);
  D_Flip_Flop d_ff_3 (.D(j_k_ff_3_q), .clk(and_1_out), .Q(BitThree), .reset(Reset));  // open: Qn, preset
  J_K_Flip_Flop j_k_ff_4 (.J(and_4_out), .K(and_4_out), .clk(CLK), .Q(JKEight), .reset(or_1_out));  // open: Qn, preset
  and and_5 (and_5_out, JKTwo, JKEight);
  or or_1 (or_1_out, and_5_out, Reset);
  D_Flip_Flop d_ff_4 (.D(JKEight), .clk(and_1_out), .Q(BitFour), .reset(Reset));  // open: Qn, preset

  assign HEX = {BitFour, BitThree, BitTwo, BitOne};
  assign ResetOut = Reset;

  // Notes on the sheet:
  //   Avoids illegal state
  //   OR for reset
endmodule

module ThreeBitCounterModulo6 (
  input  Reset,
  input  IncrementOne,
  input  IncrementTwo,
  input  CLK,
  output ResetOut,
  output [3:0] HEX,
  output JKTwo,
  output JkThree,
  output BitOne,
  output BitTwo,
  output BitThree
);

  wire and_1_out, and_2_out, and_3_out, j_k_ff_1_q, or_1_out;

  and and_1 (and_1_out, IncrementOne, IncrementTwo);
  J_K_Flip_Flop j_k_ff_1 (
    .J(and_1_out), .K(and_1_out), .clk(and_1_out), .Q(j_k_ff_1_q), .reset(or_1_out));  // open: Qn, preset
  D_Flip_Flop d_ff_1 (.D(j_k_ff_1_q), .clk(CLK), .Q(BitOne), .reset(Reset));  // open: Qn, preset
  J_K_Flip_Flop j_k_ff_2 (
    .J(j_k_ff_1_q), .K(j_k_ff_1_q), .clk(and_1_out), .Q(JKTwo), .reset(or_1_out));  // open: Qn, preset
  D_Flip_Flop d_ff_2 (.D(JKTwo), .clk(CLK), .Q(BitTwo), .reset(Reset));  // open: Qn, preset
  J_K_Flip_Flop j_k_ff_3 (
    .J(and_2_out), .K(and_2_out), .clk(and_1_out), .Q(JkThree), .reset(or_1_out));  // open: Qn, preset
  and and_2 (and_2_out, j_k_ff_1_q, JKTwo);
  D_Flip_Flop d_ff_3 (.D(JkThree), .clk(CLK), .Q(BitThree), .reset(Reset));  // open: Qn, preset
  and and_3 (and_3_out, JKTwo, JkThree);
  or or_1 (or_1_out, and_3_out, Reset);

  assign HEX = {1'b0, BitThree, BitTwo, BitOne};
  assign ResetOut = Reset;

  // Notes on the sheet:
  //   Seconds 02
  //   OR for reset
endmodule

module FourBitASyncRegister (
  input  BitOne,
  input  BitTwo,
  input  BitThree,
  input  BitFour,
  input  Reset,
  input  Split,
  output BitFourOut,
  output BitThreeOut,
  output BitTwoOut,
  output BitOneOut,
  output [3:0] HEX
);

  D_Flip_Flop d_ff_1 (.D(BitOne), .clk(Split), .Q(BitOneOut), .reset(Reset));  // open: Qn, preset
  D_Flip_Flop d_ff_2 (.D(BitTwo), .clk(Split), .Q(BitTwoOut), .reset(Reset));  // open: Qn, preset
  D_Flip_Flop d_ff_3 (.D(BitThree), .clk(Split), .Q(BitThreeOut), .reset(Reset));  // open: Qn, preset
  D_Flip_Flop d_ff_4 (.D(BitFour), .clk(Split), .Q(BitFourOut), .reset(Reset));  // open: Qn, preset

  assign HEX = {BitFourOut, BitThreeOut, BitTwoOut, BitOneOut};
endmodule

module ThreeBitASyncRegister (
  input  BitOne,
  input  BitTwo,
  input  BitThree,
  input  Reset,
  input  Split,
  output BitThreeOut,
  output BitTwoOut,
  output BitOneOut,
  output [3:0] HEX
);

  D_Flip_Flop d_ff_1 (.D(BitOne), .clk(Split), .Q(BitOneOut), .reset(Reset));  // open: Qn, preset
  D_Flip_Flop d_ff_2 (.D(BitTwo), .clk(Split), .Q(BitTwoOut), .reset(Reset));  // open: Qn, preset
  D_Flip_Flop d_ff_3 (.D(BitThree), .clk(Split), .Q(BitThreeOut), .reset(Reset));  // open: Qn, preset

  assign HEX = {1'b0, BitThreeOut, BitTwoOut, BitOneOut};
endmodule
